// Logisim project hellosemi.circ as structural Verilog: 34 circuits, main circuit main
module main (
  input  in_1,
  input  in_2,
  input  in_3,
  input  in_4,
  input  in_5,
  input  in_6,
  input  in_7,
  input  in_8,
  input  in_9,
  input  in_10,
  input  in_11,
  input  in_12,
  input  in_13,
  input  in_14,
  input  in_15,
  input  in_16,
  input  in_17,
  input  in_18,
  input  in_19,
  input  in_20,
  input  in_21,
  input  in_22,
  input  in_23,
  input  in_24,
  input  in_25,
  input  in_26,
  input  in_27,
  output out_28,
  output out_29,
  output out_30,
  output out_31,
  output out_32,
  output out_33,
  output out_34,
  output out_35,
  output out_36,
  output out_37,
  output out_38,
  output out_39,
  output out_40,
  output out_41
);

  wire and_1_out, and_3_out, d_ff_1_qn, nand_1_out, nand_2_out, nand_3_out, nor_1_out, not_1_out, not_2_out,
       not_3_out, not_4_out, not_5_out, not_6_out, not_7_out, not_8_out, not_9_out, not_10_out, or_1_out,
       taffy_out, Test_out, transistor_3_out, transistor_7_out, transistor_11_out, transistor_12_out,
       transistor_15_out, transistor_16_out, transistor_17_out, transistor_21_out, transistor_22_out,
       transistor_25_out, transistor_28_out, transistor_37_out, undriven, undriven_2;

  not not_1 (not_1_out, in_4);
  not not_2 (not_2_out, in_1);
  not not_3 (not_3_out, in_2);
  not not_4 (not_4_out, in_3);
  not not_5 (not_5_out, not_1_out);
  Transistor transistor_1 (.in(1'b1), .out(out_31), .gate(in_5));
  Transistor #(.\type ("n")) transistor_2 (.in(1'b0), .out(out_31), .gate(in_5));
  Transistor transistor_3 (.in(1'b1), .out(transistor_3_out), .gate(in_8));
  Transistor #(.\type ("n")) transistor_4 (.in(1'b0), .out(transistor_3_out), .gate(in_8));
  Transistor transistor_5 (.in(1'b1), .out(out_33), .gate(in_10));
  Transistor #(.\type ("n")) transistor_6 (.in(1'b0), .out(out_36), .gate(in_14));
  not not_6 (not_6_out, in_18);
  not not_7 (not_7_out, in_22);
  or or_1 (or_1_out, in_24, in_25);
  nand nand_1 (nand_1_out, in_24, in_25);
  and Test (Test_out, not_2_out, in_2);
  and taffy (taffy_out, in_1, not_3_out);
  and and_1 (and_1_out, not_4_out, in_3);
  not not_8 (not_8_out, not_5_out);
  not not_9 (not_9_out, not_8_out);
  Transistor transistor_7 (.in(1'b1), .out(transistor_7_out), .gate(in_9));
  Transistor #(.\type ("n")) transistor_8 (.in(1'b0), .out(transistor_7_out), .gate(in_9));
  Transistor transistor_9 (.in(1'b1), .out(out_33), .gate(in_12));
  Transistor #(.\type ("n")) transistor_10 (.in(transistor_11_out), .out(out_33), .gate(in_10));
  Transistor #(.\type ("n")) transistor_11 (.in(1'b0), .out(transistor_11_out), .gate(in_12));
  Transistor transistor_12 (.in(1'b1), .out(transistor_12_out), .gate(in_14));
  Transistor transistor_13 (.in(transistor_12_out), .out(out_36), .gate(in_16));
  Transistor #(.\type ("n")) transistor_14 (.in(1'b0), .out(out_36), .gate(in_16));
  nand nand_2 (nand_2_out, not_6_out, in_22);
  nand nand_3 (nand_3_out, in_18, not_7_out);
  nand nand_4 (out_41, or_1_out, nand_1_out);
  or or_2 (out_28, Test_out, taffy_out);
  D_Flip_Flop d_ff_1 (
    .D(d_ff_1_qn), .clk(and_1_out), .Q(out_29), .Qn(d_ff_1_qn), .preset(undriven), .reset(undriven_2));
  not not_10 (not_10_out, not_9_out);
  and and_2 (out_30, not_10_out, in_4);
  nand nand_5 (out_39, nand_2_out, nand_3_out);
  Transistor transistor_15 (.in(1'b1), .out(transistor_15_out), .gate(in_11));
  Transistor #(.\type ("n")) transistor_16 (.in(1'b0), .out(transistor_16_out), .gate(in_15));
  Transistor transistor_17 (.in(1'b1), .out(transistor_17_out), .gate(in_26));
  Transistor #(.\type ("n")) transistor_18 (.in(1'b0), .out(transistor_17_out), .gate(in_26));
  Transistor transistor_19 (.in(1'b1), .out(transistor_15_out), .gate(in_13));
  Transistor #(.\type ("n")) transistor_20 (.in(transistor_21_out), .out(transistor_15_out), .gate(in_11));
  Transistor #(.\type ("n")) transistor_21 (.in(1'b0), .out(transistor_21_out), .gate(in_13));
  Transistor transistor_22 (.in(1'b1), .out(transistor_22_out), .gate(in_15));
  Transistor transistor_23 (.in(transistor_22_out), .out(transistor_16_out), .gate(in_17));
  Transistor #(.\type ("n")) transistor_24 (.in(1'b0), .out(transistor_16_out), .gate(in_17));
  nor nor_1 (nor_1_out, in_19, in_23);
  and and_3 (and_3_out, in_19, in_23);
  Transistor transistor_25 (.in(1'b1), .out(transistor_25_out), .gate(in_6));
  Transistor transistor_26 (.in(transistor_25_out), .out(out_32), .gate(in_7));
  Transistor #(.\type ("n")) transistor_27 (.in(transistor_28_out), .out(out_32), .gate(in_7));
  Transistor #(.\type ("n")) transistor_28 (.in(1'b0), .out(transistor_28_out), .gate(in_6));
  Transistor transistor_29 (.in(1'b1), .out(out_34), .gate(transistor_15_out));
  Transistor #(.\type ("n")) transistor_30 (.in(1'b0), .out(out_34), .gate(transistor_15_out));
  Transistor transistor_31 (.in(1'b1), .out(out_35), .gate(transistor_16_out));
  Transistor #(.\type ("n")) transistor_32 (.in(1'b0), .out(out_35), .gate(transistor_16_out));
  Transistor transistor_33 (.in(in_27), .out(out_40), .gate(transistor_17_out));
  Transistor transistor_34 (.in(transistor_17_out), .out(out_40), .gate(in_27));
  Transistor #(.\type ("n")) transistor_35 (.in(in_26), .out(out_40), .gate(in_27));
  Transistor #(.\type ("n")) transistor_36 (.in(in_27), .out(out_40), .gate(in_26));
  nor nor_2 (out_38, nor_1_out, and_3_out);
  Transistor transistor_37 (.in(1'b1), .out(transistor_37_out), .gate(in_20));
  Transistor #(.\type ("n")) transistor_38 (.in(1'b0), .out(transistor_37_out), .gate(in_20));
  Transistor transistor_39 (.in(in_20), .out(out_37), .gate(in_21));
  Transistor #(.\type ("n")) transistor_40 (.in(transistor_37_out), .out(out_37), .gate(in_21));
  Transistor transistor_41 (.in(in_21), .out(out_37), .gate(in_20));
  Transistor #(.\type ("n")) transistor_42 (.in(in_21), .out(out_37), .gate(transistor_37_out));

  // Notes on the sheet:
  //   反相器
  //   反相器并联
  //   同或门-14
  //   与非门-串联nMOS
  //   或非门-串联pMOS
  //   异或门-16
  //   异或门-14
  //   反相器串联
  //   与门-串联nMOS
  //   或门-串联pMOS
  //   同或门-全定制
  //   异或门-全定制
endmodule

module decoder2to4 (
  input  in_1,
  input  in_2,
  output out_3,
  output out_4,
  output out_5,
  output out_6
);

  wire not_1_out, not_2_out;

  not not_1 (not_1_out, in_1);
  not not_2 (not_2_out, in_2);
  and and_1 (out_3, not_1_out, not_2_out);
  and and_2 (out_4, not_1_out, in_2);
  and and_3 (out_5, in_1, not_2_out);
  and and_4 (out_6, in_1, in_2);

  // Notes on the sheet:
  //   2-4译码器
endmodule

module decoder3to8 (
  input  in_1,
  input  in_2,
  input  in_3,
  output out_4,
  output out_5,
  output out_6,
  output out_7,
  output out_8,
  output out_9,
  output out_10,
  output out_11
);

  wire decoder2to4_1_out_3, decoder2to4_1_out_4, decoder2to4_1_out_5, decoder2to4_1_out_6,
       decoder2to4_2_out_3, decoder2to4_2_out_4, decoder2to4_2_out_5, decoder2to4_2_out_6, not_1_out;

  decoder2to4 decoder2to4_1 (
    .in_1(in_2), .in_2(in_3), .out_3(decoder2to4_1_out_3), .out_4(decoder2to4_1_out_4),
    .out_5(decoder2to4_1_out_5), .out_6(decoder2to4_1_out_6));
  decoder2to4 decoder2to4_2 (
    .in_1(in_2), .in_2(in_3), .out_3(decoder2to4_2_out_3), .out_4(decoder2to4_2_out_4),
    .out_5(decoder2to4_2_out_5), .out_6(decoder2to4_2_out_6));
  not not_1 (not_1_out, in_1);
  and and_1 (out_4, decoder2to4_1_out_3, not_1_out);
  and and_2 (out_5, decoder2to4_1_out_4, not_1_out);
  and and_3 (out_6, decoder2to4_1_out_5, not_1_out);
  and and_4 (out_7, decoder2to4_1_out_6, not_1_out);
  and and_5 (out_8, decoder2to4_2_out_3, in_1);
  and and_6 (out_9, decoder2to4_2_out_4, in_1);
  and and_7 (out_10, decoder2to4_2_out_5, in_1);
  and and_8 (out_11, decoder2to4_2_out_6, in_1);

  // Notes on the sheet:
  //   TODO：改成位宽形式简化电路
endmodule

module decoder3to8new (
  input  [2:0] in_1,
  output [7:0] out_2
);

  wire not_1_out;
  wire [3:0] bit_extender_1_out, bit_extender_2_out;
  wire [7:0] decoder2to4_1_out_3;

  not not_1 (not_1_out, in_1[2]);
  assign bit_extender_1_out = {{3{not_1_out}}, not_1_out};  // Bit_Extender bit_extender_1
  assign bit_extender_2_out = {{3{in_1[2]}}, in_1[2]};  // Bit_Extender bit_extender_2
  decoder2to4 decoder2to4_1 (
    .in_1(in_1[1]), .in_2(in_1[0]), .out_3(decoder2to4_1_out_3[0]), .out_4(decoder2to4_1_out_3[1]),
    .out_5(decoder2to4_1_out_3[2]), .out_6(decoder2to4_1_out_3[3]));
  decoder2to4 decoder2to4_2 (
    .in_1(in_1[1]), .in_2(in_1[0]), .out_3(decoder2to4_1_out_3[4]), .out_4(decoder2to4_1_out_3[5]),
    .out_5(decoder2to4_1_out_3[6]), .out_6(decoder2to4_1_out_3[7]));
  assign out_2 = {bit_extender_2_out, bit_extender_1_out} & decoder2to4_1_out_3;  // AND_Gate and_1, 8 bits wide
endmodule

module sigment7 (
  input  [3:0] in_1
);

  wire demultiplexer_1_out0, demultiplexer_1_out1, demultiplexer_1_out2, demultiplexer_1_out3,
       demultiplexer_1_out4, demultiplexer_1_out5, demultiplexer_1_out6, demultiplexer_1_out7,
       demultiplexer_1_out8, demultiplexer_1_out9, demultiplexer_1_out10, demultiplexer_1_out11,
       demultiplexer_1_out12, demultiplexer_1_out13, demultiplexer_1_out14, demultiplexer_1_out15, or_1_out,
       or_2_out, or_3_out, or_4_out, or_5_out, or_6_out, or_7_out, or_8_out;

  Demultiplexer #(.select(4)) demultiplexer_1 (
    .out0(demultiplexer_1_out0), .out1(demultiplexer_1_out1), .out2(demultiplexer_1_out2),
    .out3(demultiplexer_1_out3), .out4(demultiplexer_1_out4), .out5(demultiplexer_1_out5),
    .out6(demultiplexer_1_out6), .out7(demultiplexer_1_out7), .out8(demultiplexer_1_out8),
    .out9(demultiplexer_1_out9), .out10(demultiplexer_1_out10), .out11(demultiplexer_1_out11),
    .out12(demultiplexer_1_out12), .out13(demultiplexer_1_out13), .out14(demultiplexer_1_out14),
    .out15(demultiplexer_1_out15), .in(1'b1), .sel(in_1));
  or or_1 (or_1_out, demultiplexer_1_out0, demultiplexer_1_out4, demultiplexer_1_out5, demultiplexer_1_out6, demultiplexer_1_out8, demultiplexer_1_out9);
  or or_2 (or_2_out, demultiplexer_1_out0, demultiplexer_1_out2, demultiplexer_1_out3, demultiplexer_1_out5, demultiplexer_1_out6, demultiplexer_1_out7, demultiplexer_1_out8, demultiplexer_1_out9);
  or or_3 (or_3_out, demultiplexer_1_out2, demultiplexer_1_out3, demultiplexer_1_out4, demultiplexer_1_out5, demultiplexer_1_out6, demultiplexer_1_out8, demultiplexer_1_out9);
  or or_4 (or_4_out, demultiplexer_1_out0, demultiplexer_1_out1, demultiplexer_1_out2, demultiplexer_1_out3, demultiplexer_1_out4, demultiplexer_1_out7, demultiplexer_1_out8, demultiplexer_1_out9);
  or or_5 (or_5_out, demultiplexer_1_out10, demultiplexer_1_out11, demultiplexer_1_out12, demultiplexer_1_out13, demultiplexer_1_out14, demultiplexer_1_out15);
  or or_6 (or_6_out, demultiplexer_1_out0, demultiplexer_1_out1, demultiplexer_1_out3, demultiplexer_1_out4, demultiplexer_1_out5, demultiplexer_1_out6, demultiplexer_1_out7, demultiplexer_1_out8, demultiplexer_1_out9);
  or or_7 (or_7_out, demultiplexer_1_out0, demultiplexer_1_out2, demultiplexer_1_out3, demultiplexer_1_out5, demultiplexer_1_out6, demultiplexer_1_out8, demultiplexer_1_out9);
  or or_8 (or_8_out, demultiplexer_1_out0, demultiplexer_1_out2, demultiplexer_1_out6, demultiplexer_1_out8);
  _7_Segment_Display u_7_segment_display_1 (
    .g(or_3_out), .f(or_1_out), .a(or_2_out), .b(or_4_out), .e(or_8_out), .d(or_7_out), .c(or_6_out),
    .dp(or_5_out));
endmodule

module segment16 (
  input  [3:0] in_1
);

  wire or_1_out, or_2_out, or_3_out, or_4_out, or_5_out, or_6_out, or_7_out;
  wire [15:0] demultiplexer_1_out0;

  Demultiplexer #(.select(4)) demultiplexer_1 (
    .out0(demultiplexer_1_out0[0]), .out1(demultiplexer_1_out0[1]), .out2(demultiplexer_1_out0[2]),
    .out3(demultiplexer_1_out0[3]), .out4(demultiplexer_1_out0[4]), .out5(demultiplexer_1_out0[5]),
    .out6(demultiplexer_1_out0[6]), .out7(demultiplexer_1_out0[7]), .out8(demultiplexer_1_out0[8]),
    .out9(demultiplexer_1_out0[9]), .out10(demultiplexer_1_out0[10]), .out11(demultiplexer_1_out0[11]),
    .out12(demultiplexer_1_out0[12]), .out13(demultiplexer_1_out0[13]), .out14(demultiplexer_1_out0[14]),
    .out15(demultiplexer_1_out0[15]), .in(1'b1), .sel(in_1));
  or or_1 (or_1_out, demultiplexer_1_out0[15], demultiplexer_1_out0[14], demultiplexer_1_out0[12], demultiplexer_1_out0[10], demultiplexer_1_out0[9], demultiplexer_1_out0[8], demultiplexer_1_out0[7], demultiplexer_1_out0[6], demultiplexer_1_out0[5], demultiplexer_1_out0[3], demultiplexer_1_out0[2], demultiplexer_1_out0[0]);
  or or_2 (or_2_out, demultiplexer_1_out0[13], demultiplexer_1_out0[10], demultiplexer_1_out0[9], demultiplexer_1_out0[8], demultiplexer_1_out0[7], demultiplexer_1_out0[4], demultiplexer_1_out0[3], demultiplexer_1_out0[2], demultiplexer_1_out0[1], demultiplexer_1_out0[0]);
  or or_3 (or_3_out, demultiplexer_1_out0[13], demultiplexer_1_out0[11], demultiplexer_1_out0[10], demultiplexer_1_out0[9], demultiplexer_1_out0[8], demultiplexer_1_out0[7], demultiplexer_1_out0[6], demultiplexer_1_out0[5], demultiplexer_1_out0[4], demultiplexer_1_out0[3], demultiplexer_1_out0[1], demultiplexer_1_out0[0]);
  _7_Segment_Display u_7_segment_display_1 (
    .g(or_7_out), .f(or_6_out), .a(or_1_out), .b(or_2_out), .e(or_5_out), .d(or_4_out), .c(or_3_out));  // open: dp
  or or_4 (or_4_out, demultiplexer_1_out0[14], demultiplexer_1_out0[13], demultiplexer_1_out0[12], demultiplexer_1_out0[11], demultiplexer_1_out0[9], demultiplexer_1_out0[8], demultiplexer_1_out0[6], demultiplexer_1_out0[5], demultiplexer_1_out0[3], demultiplexer_1_out0[2], demultiplexer_1_out0[0]);
  or or_5 (or_5_out, demultiplexer_1_out0[15], demultiplexer_1_out0[14], demultiplexer_1_out0[13], demultiplexer_1_out0[12], demultiplexer_1_out0[11], demultiplexer_1_out0[10], demultiplexer_1_out0[8], demultiplexer_1_out0[6], demultiplexer_1_out0[2], demultiplexer_1_out0[0]);
  or or_6 (or_6_out, demultiplexer_1_out0[15], demultiplexer_1_out0[14], demultiplexer_1_out0[12], demultiplexer_1_out0[11], demultiplexer_1_out0[10], demultiplexer_1_out0[9], demultiplexer_1_out0[8], demultiplexer_1_out0[6], demultiplexer_1_out0[5], demultiplexer_1_out0[4], demultiplexer_1_out0[0]);
  or or_7 (or_7_out, demultiplexer_1_out0[15], demultiplexer_1_out0[14], demultiplexer_1_out0[13], demultiplexer_1_out0[11], demultiplexer_1_out0[10], demultiplexer_1_out0[9], demultiplexer_1_out0[8], demultiplexer_1_out0[6], demultiplexer_1_out0[5], demultiplexer_1_out0[4], demultiplexer_1_out0[3], demultiplexer_1_out0[2]);
endmodule

module encoder4to2 (
  input  A3,
  input  A2,
  input  A1,
  input  A0,
  output out_5,
  output out_6
);

  wire not_1_out, not_2_out, not_3_out, or_1_out, or_2_out, or_3_out, or_4_out;

  not not_1 (not_1_out, A1);
  not not_2 (not_2_out, A3);
  not not_3 (not_3_out, A2);
  or or_1 (or_1_out, A3, not_3_out, A1, A0);
  or or_2 (or_2_out, not_2_out, A2, A1, A0);
  or or_3 (or_3_out, not_2_out, A2, A1, A0);
  or or_4 (or_4_out, A3, A2, not_1_out, A0);
  nand nand_1 (out_5, or_1_out, or_2_out);
  nand nand_2 (out_6, or_3_out, or_4_out);
endmodule

module encoder4to2prior (
  input  A3,
  input  A2,
  input  A1,
  input  A0,
  output out_5,
  output out_6
);

  wire and_1_out, and_2_out, and_3_out, and_4_out, and_5_out, and_6_out, not_1_out, not_2_out, not_3_out,
       not_4_out, not_5_out, not_6_out, or_1_out, or_2_out, or_3_out, or_4_out;

  not not_1 (not_1_out, A3);
  and and_1 (and_1_out, not_1_out, A2);
  not not_2 (not_2_out, and_1_out);
  and and_2 (and_2_out, not_1_out, A1);
  and and_3 (and_3_out, not_1_out, A0);
  and and_4 (and_4_out, not_2_out, and_2_out);
  and and_5 (and_5_out, not_2_out, and_3_out);
  not not_3 (not_3_out, and_4_out);
  and and_6 (and_6_out, not_3_out, and_5_out);
  not not_4 (not_4_out, and_4_out);
  not not_5 (not_5_out, A3);
  not not_6 (not_6_out, and_1_out);
  or or_1 (or_1_out, A3, not_6_out, and_4_out, and_6_out);
  or or_2 (or_2_out, not_5_out, and_1_out, and_4_out, and_6_out);
  or or_3 (or_3_out, not_5_out, and_1_out, and_4_out, and_6_out);
  or or_4 (or_4_out, A3, and_1_out, not_4_out, and_6_out);
  nand nand_1 (out_5, or_1_out, or_2_out);
  nand nand_2 (out_6, or_3_out, or_4_out);
endmodule

module encoder16to4prior (
  input  in_1,
  input  in_2,
  input  in_3,
  input  in_4,
  input  in_5,
  input  in_6,
  input  in_7,
  input  in_8,
  input  in_9,
  input  in_10,
  input  in_11,
  input  in_12,
  input  in_13,
  input  in_14,
  input  in_15,
  input  in_16,
  input  in_17,
  input  in_18,
  input  in_19,
  input  in_20,
  input  in_21,
  input  in_22,
  input  in_23,
  input  in_24,
  input  in_25,
  input  in_26,
  input  in_27,
  input  in_28,
  input  in_29,
  input  in_30,
  input  in_31,
  input  in_32
);

  wire and_10_out, and_11_out, and_13_out, and_14_out, and_16_out, and_18_out, not_1_out, not_2_out,
       not_3_out, not_4_out, not_5_out, not_6_out, or_4_out, or_5_out, or_6_out, or_8_out, or_9_out,
       or_10_out, or_11_out, or_12_out, or_13_out, or_14_out, or_15_out, or_16_out, or_17_out, or_18_out,
       or_19_out, or_20_out, or_21_out, or_22_out, or_23_out, or_24_out;
  wire [1:0] and_1_out, and_2_out, and_3_out, and_4_out, and_5_out, and_6_out, and_7_out, and_8_out,
       encoder4to2prior_1_out_5, encoder4to2prior_2_out_5, encoder4to2prior_3_out_5,
       encoder4to2prior_4_out_5, int0123_out_6, int4567_out_6, int891011_out_6, int12131415_out_6;
  wire [1:1] and_9_out, and_12_out, and_15_out, and_17_out, and_19_out, and_20_out, or_3_out, or_7_out;
  wire [3:0] or_1_out, or_2_out;
  wire [15:0] demultiplexer_1_out0, demultiplexer_2_out0;

  encoder4to2prior encoder4to2prior_1 (
    .A3(in_17), .A2(in_18), .A1(in_19), .A0(in_20), .out_5(encoder4to2prior_1_out_5[0]),
    .out_6(encoder4to2prior_1_out_5[1]));
  assign and_1_out = encoder4to2prior_1_out_5 & {2{or_7_out[1]}};  // AND_Gate and_1, 2 bits wide
  assign {or_1_out[0], or_1_out[1]} = and_1_out | and_2_out | and_7_out | and_8_out;  // OR_Gate or_1, 2 bits wide
  encoder4to2prior int12131415 (
    .A3(in_1), .A2(in_2), .A1(in_3), .A0(in_4), .out_5(int12131415_out_6[1]), .out_6(int12131415_out_6[0]));
  encoder4to2prior int891011 (
    .A3(in_5), .A2(in_6), .A1(in_7), .A0(in_8), .out_5(int891011_out_6[1]), .out_6(int891011_out_6[0]));
  encoder4to2prior int4567 (
    .A3(in_9), .A2(in_10), .A1(in_11), .A0(in_12), .out_5(int4567_out_6[1]), .out_6(int4567_out_6[0]));
  encoder4to2prior int0123 (
    .A3(in_13), .A2(in_14), .A1(in_15), .A0(in_16), .out_5(int0123_out_6[1]), .out_6(int0123_out_6[0]));
  encoder4to2prior encoder4to2prior_2 (
    .A3(in_21), .A2(in_22), .A1(in_23), .A0(in_24), .out_5(encoder4to2prior_2_out_5[0]),
    .out_6(encoder4to2prior_2_out_5[1]));
  // Probe on encoder4to2prior_2_out_5
  assign and_2_out = encoder4to2prior_2_out_5 & {2{and_12_out[1]}};  // AND_Gate and_2, 2 bits wide
  // Probe on int12131415_out_6
  assign and_3_out = int891011_out_6 & {2{and_9_out[1]}};  // AND_Gate and_3, 2 bits wide
  assign and_4_out = int12131415_out_6 & {2{or_3_out[1]}};  // AND_Gate and_4, 2 bits wide
  encoder4to2prior encoder4to2prior_3 (
    .A3(in_25), .A2(in_26), .A1(in_27), .A0(in_28), .out_5(encoder4to2prior_3_out_5[0]),
    .out_6(encoder4to2prior_3_out_5[1]));
  assign and_5_out = int0123_out_6 & {2{and_19_out[1]}};  // AND_Gate and_5, 2 bits wide
  assign and_6_out = int4567_out_6 & {2{and_15_out[1]}};  // AND_Gate and_6, 2 bits wide
  assign or_2_out[1:0] = and_4_out | and_3_out | and_6_out | and_5_out;  // OR_Gate or_2, 2 bits wide
  // Probe on encoder4to2prior_3_out_5
  assign and_7_out = encoder4to2prior_3_out_5 & {2{and_17_out[1]}};  // AND_Gate and_7, 2 bits wide
  encoder4to2prior encoder4to2prior_4 (
    .A3(in_29), .A2(in_30), .A1(in_31), .A0(in_32), .out_5(encoder4to2prior_4_out_5[0]),
    .out_6(encoder4to2prior_4_out_5[1]));
  assign and_8_out = encoder4to2prior_4_out_5 & {2{and_20_out[1]}};  // AND_Gate and_8, 2 bits wide
  or or_3 (or_3_out[1], int12131415_out_6[1], int12131415_out_6[0]);
  not not_1 (not_1_out, or_3_out[1]);
  or or_4 (or_4_out, int891011_out_6[1], int891011_out_6[0]);
  or or_5 (or_5_out, int4567_out_6[1], int4567_out_6[0]);
  or or_6 (or_6_out, int0123_out_6[1], int0123_out_6[0]);
  or or_7 (or_7_out[1], in_17, in_18, in_19, in_20);
  or or_8 (or_8_out, in_21, in_22, in_23, in_24);
  or or_9 (or_9_out, in_25, in_26, in_27, in_28);
  or or_10 (or_10_out, in_29, in_30, in_31, in_32);
  and and_9 (and_9_out[1], not_1_out, or_4_out);
  and and_10 (and_10_out, not_1_out, or_5_out);
  and and_11 (and_11_out, not_1_out, or_6_out);
  not not_2 (not_2_out, or_7_out[1]);
  and and_12 (and_12_out[1], not_2_out, or_8_out);
  and and_13 (and_13_out, not_2_out, or_9_out);
  and and_14 (and_14_out, not_2_out, or_10_out);
  not not_3 (not_3_out, and_9_out[1]);
  and and_15 (and_15_out[1], not_3_out, and_10_out);
  and and_16 (and_16_out, not_3_out, and_11_out);
  not not_4 (not_4_out, and_12_out[1]);
  not not_5 (not_5_out, and_15_out[1]);
  and and_17 (and_17_out[1], not_4_out, and_13_out);
  and and_18 (and_18_out, not_4_out, and_14_out);
  and and_19 (and_19_out[1], not_5_out, and_16_out);
  not not_6 (not_6_out, and_17_out[1]);
  and and_20 (and_20_out[1], not_6_out, and_18_out);
  // Probe on or_2_out[1:0]
  encoder4to2prior encoder4to2prior_5 (
    .A3(or_3_out[1]), .A2(and_9_out[1]), .A1(and_15_out[1]), .A0(and_19_out[1]), .out_5(or_2_out[3]),
    .out_6(or_2_out[2]));
  encoder4to2prior encoder4to2prior_6 (
    .A3(or_7_out[1]), .A2(and_12_out[1]), .A1(and_17_out[1]), .A0(and_20_out[1]), .out_5(or_1_out[3]),
    .out_6(or_1_out[2]));
  Demultiplexer #(.select(4)) demultiplexer_1 (
    .out0(demultiplexer_1_out0[0]), .out1(demultiplexer_1_out0[1]), .out2(demultiplexer_1_out0[2]),
    .out3(demultiplexer_1_out0[3]), .out4(demultiplexer_1_out0[4]), .out5(demultiplexer_1_out0[5]),
    .out6(demultiplexer_1_out0[6]), .out7(demultiplexer_1_out0[7]), .out8(demultiplexer_1_out0[8]),
    .out9(demultiplexer_1_out0[9]), .out10(demultiplexer_1_out0[10]), .out11(demultiplexer_1_out0[11]),
    .out12(demultiplexer_1_out0[12]), .out13(demultiplexer_1_out0[13]), .out14(demultiplexer_1_out0[14]),
    .out15(demultiplexer_1_out0[15]), .in(1'b1), .sel(or_2_out));
  Demultiplexer #(.select(4)) demultiplexer_2 (
    .out0(demultiplexer_2_out0[0]), .out1(demultiplexer_2_out0[1]), .out2(demultiplexer_2_out0[2]),
    .out3(demultiplexer_2_out0[3]), .out4(demultiplexer_2_out0[4]), .out5(demultiplexer_2_out0[5]),
    .out6(demultiplexer_2_out0[6]), .out7(demultiplexer_2_out0[7]), .out8(demultiplexer_2_out0[8]),
    .out9(demultiplexer_2_out0[9]), .out10(demultiplexer_2_out0[10]), .out11(demultiplexer_2_out0[11]),
    .out12(demultiplexer_2_out0[12]), .out13(demultiplexer_2_out0[13]), .out14(demultiplexer_2_out0[14]),
    .out15(demultiplexer_2_out0[15]), .in(1'b1), .sel(or_1_out));
  or or_11 (or_11_out, demultiplexer_1_out0[15], demultiplexer_1_out0[14], demultiplexer_1_out0[12], demultiplexer_1_out0[10], demultiplexer_1_out0[9], demultiplexer_1_out0[8], demultiplexer_1_out0[7], demultiplexer_1_out0[6], demultiplexer_1_out0[5], demultiplexer_1_out0[3], demultiplexer_1_out0[2], demultiplexer_1_out0[0]);
  or or_12 (or_12_out, demultiplexer_2_out0[15], demultiplexer_2_out0[14], demultiplexer_2_out0[12], demultiplexer_2_out0[10], demultiplexer_2_out0[9], demultiplexer_2_out0[8], demultiplexer_2_out0[7], demultiplexer_2_out0[6], demultiplexer_2_out0[5], demultiplexer_2_out0[3], demultiplexer_2_out0[2], demultiplexer_2_out0[0]);
  or or_13 (or_13_out, demultiplexer_1_out0[13], demultiplexer_1_out0[10], demultiplexer_1_out0[9], demultiplexer_1_out0[8], demultiplexer_1_out0[7], demultiplexer_1_out0[4], demultiplexer_1_out0[3], demultiplexer_1_out0[2], demultiplexer_1_out0[1], demultiplexer_1_out0[0]);
  or or_14 (or_14_out, demultiplexer_2_out0[13], demultiplexer_2_out0[10], demultiplexer_2_out0[9], demultiplexer_2_out0[8], demultiplexer_2_out0[7], demultiplexer_2_out0[4], demultiplexer_2_out0[3], demultiplexer_2_out0[2], demultiplexer_2_out0[1], demultiplexer_2_out0[0]);
  or or_15 (or_15_out, demultiplexer_1_out0[13], demultiplexer_1_out0[11], demultiplexer_1_out0[10], demultiplexer_1_out0[9], demultiplexer_1_out0[8], demultiplexer_1_out0[7], demultiplexer_1_out0[6], demultiplexer_1_out0[5], demultiplexer_1_out0[4], demultiplexer_1_out0[3], demultiplexer_1_out0[1], demultiplexer_1_out0[0]);
  or or_16 (or_16_out, demultiplexer_2_out0[13], demultiplexer_2_out0[11], demultiplexer_2_out0[10], demultiplexer_2_out0[9], demultiplexer_2_out0[8], demultiplexer_2_out0[7], demultiplexer_2_out0[6], demultiplexer_2_out0[5], demultiplexer_2_out0[4], demultiplexer_2_out0[3], demultiplexer_2_out0[1], demultiplexer_2_out0[0]);
  _7_Segment_Display u_7_segment_display_1 (
    .g(or_23_out), .f(or_21_out), .a(or_11_out), .b(or_13_out), .e(or_19_out), .d(or_17_out), .c(or_15_out));  // open: dp
  _7_Segment_Display u_7_segment_display_2 (
    .g(or_24_out), .f(or_22_out), .a(or_12_out), .b(or_14_out), .e(or_20_out), .d(or_18_out), .c(or_16_out));  // open: dp
  or or_17 (or_17_out, demultiplexer_1_out0[14], demultiplexer_1_out0[13], demultiplexer_1_out0[12], demultiplexer_1_out0[11], demultiplexer_1_out0[9], demultiplexer_1_out0[8], demultiplexer_1_out0[6], demultiplexer_1_out0[5], demultiplexer_1_out0[3], demultiplexer_1_out0[2], demultiplexer_1_out0[0]);
  or or_18 (or_18_out, demultiplexer_2_out0[14], demultiplexer_2_out0[13], demultiplexer_2_out0[12], demultiplexer_2_out0[11], demultiplexer_2_out0[9], demultiplexer_2_out0[8], demultiplexer_2_out0[6], demultiplexer_2_out0[5], demultiplexer_2_out0[3], demultiplexer_2_out0[2], demultiplexer_2_out0[0]);
  or or_19 (or_19_out, demultiplexer_1_out0[15], demultiplexer_1_out0[14], demultiplexer_1_out0[13], demultiplexer_1_out0[12], demultiplexer_1_out0[11], demultiplexer_1_out0[10], demultiplexer_1_out0[8], demultiplexer_1_out0[6], demultiplexer_1_out0[2], demultiplexer_1_out0[0]);
  or or_20 (or_20_out, demultiplexer_2_out0[15], demultiplexer_2_out0[14], demultiplexer_2_out0[13], demultiplexer_2_out0[12], demultiplexer_2_out0[11], demultiplexer_2_out0[10], demultiplexer_2_out0[8], demultiplexer_2_out0[6], demultiplexer_2_out0[2], demultiplexer_2_out0[0]);
  or or_21 (or_21_out, demultiplexer_1_out0[15], demultiplexer_1_out0[14], demultiplexer_1_out0[12], demultiplexer_1_out0[11], demultiplexer_1_out0[10], demultiplexer_1_out0[9], demultiplexer_1_out0[8], demultiplexer_1_out0[6], demultiplexer_1_out0[5], demultiplexer_1_out0[4], demultiplexer_1_out0[0]);
  or or_22 (or_22_out, demultiplexer_2_out0[15], demultiplexer_2_out0[14], demultiplexer_2_out0[12], demultiplexer_2_out0[11], demultiplexer_2_out0[10], demultiplexer_2_out0[9], demultiplexer_2_out0[8], demultiplexer_2_out0[6], demultiplexer_2_out0[5], demultiplexer_2_out0[4], demultiplexer_2_out0[0]);
  or or_23 (or_23_out, demultiplexer_1_out0[15], demultiplexer_1_out0[14], demultiplexer_1_out0[13], demultiplexer_1_out0[11], demultiplexer_1_out0[10], demultiplexer_1_out0[9], demultiplexer_1_out0[8], demultiplexer_1_out0[6], demultiplexer_1_out0[5], demultiplexer_1_out0[4], demultiplexer_1_out0[3], demultiplexer_1_out0[2]);
  or or_24 (or_24_out, demultiplexer_2_out0[15], demultiplexer_2_out0[14], demultiplexer_2_out0[13], demultiplexer_2_out0[11], demultiplexer_2_out0[10], demultiplexer_2_out0[9], demultiplexer_2_out0[8], demultiplexer_2_out0[6], demultiplexer_2_out0[5], demultiplexer_2_out0[4], demultiplexer_2_out0[3], demultiplexer_2_out0[2]);

  // Notes on the sheet:
  //   失败设计案例：4、8、C无法输出
endmodule

module multiplexer2to1 (
  input  S,
  input  D0,
  input  D1,
  output out_4
);

  wire and_1_out, and_2_out, not_1_out;

  not not_1 (not_1_out, S);
  and and_1 (and_1_out, S, D0);
  and and_2 (and_2_out, not_1_out, D1);
  or or_1 (out_4, and_1_out, and_2_out);
endmodule

module MUX_4to1_3bit (
  input  [1:0] S,
  input  [2:0] D0,
  input  [2:0] D1,
  input  [2:0] D2,
  input  [2:0] D3,
  output [2:0] Y
);

  wire [2:0] and_1_out, and_2_out, and_3_out, and_4_out;
  wire [2:2] decoder_1_out0, decoder_1_out1, decoder_1_out2, decoder_1_out3;

  Decoder #(.select(2)) decoder_1 (
    .out0(decoder_1_out0[2]), .out1(decoder_1_out1[2]), .out2(decoder_1_out2[2]), .out3(decoder_1_out3[2]),
    .sel(S));  // open: en
  assign and_1_out = D0 & {3{decoder_1_out0[2]}};  // AND_Gate and_1, 3 bits wide
  assign and_2_out = D1 & {3{decoder_1_out1[2]}};  // AND_Gate and_2, 3 bits wide
  assign and_3_out = D2 & {3{decoder_1_out2[2]}};  // AND_Gate and_3, 3 bits wide
  assign Y = and_1_out | and_2_out | and_3_out | and_4_out;  // OR_Gate or_1, 3 bits wide
  assign and_4_out = D3 & {3{decoder_1_out3[2]}};  // AND_Gate and_4, 3 bits wide
endmodule

module sigment10or16 (
  input  [3:0] in_1,
  input  in_2
);

  wire [7:0] multiplexer_1_out, point_out;
  wire [7:1] GG_out;
  wire [15:0] demultiplexer_1_out0;

  Demultiplexer #(.select(4)) demultiplexer_1 (
    .out0(demultiplexer_1_out0[0]), .out1(demultiplexer_1_out0[1]), .out2(demultiplexer_1_out0[2]),
    .out3(demultiplexer_1_out0[3]), .out4(demultiplexer_1_out0[4]), .out5(demultiplexer_1_out0[5]),
    .out6(demultiplexer_1_out0[6]), .out7(demultiplexer_1_out0[7]), .out8(demultiplexer_1_out0[8]),
    .out9(demultiplexer_1_out0[9]), .out10(demultiplexer_1_out0[10]), .out11(demultiplexer_1_out0[11]),
    .out12(demultiplexer_1_out0[12]), .out13(demultiplexer_1_out0[13]), .out14(demultiplexer_1_out0[14]),
    .out15(demultiplexer_1_out0[15]), .in(1'b1), .sel(in_1));
  or F (point_out[2], demultiplexer_1_out0[0], demultiplexer_1_out0[4], demultiplexer_1_out0[5], demultiplexer_1_out0[6], demultiplexer_1_out0[8], demultiplexer_1_out0[9]);
  or A (point_out[7], demultiplexer_1_out0[0], demultiplexer_1_out0[2], demultiplexer_1_out0[3], demultiplexer_1_out0[5], demultiplexer_1_out0[6], demultiplexer_1_out0[7], demultiplexer_1_out0[8], demultiplexer_1_out0[9]);
  or G (point_out[1], demultiplexer_1_out0[2], demultiplexer_1_out0[3], demultiplexer_1_out0[4], demultiplexer_1_out0[5], demultiplexer_1_out0[6], demultiplexer_1_out0[8], demultiplexer_1_out0[9]);
  or B (point_out[6], demultiplexer_1_out0[0], demultiplexer_1_out0[1], demultiplexer_1_out0[2], demultiplexer_1_out0[3], demultiplexer_1_out0[4], demultiplexer_1_out0[7], demultiplexer_1_out0[8], demultiplexer_1_out0[9]);
  or point (point_out[0], demultiplexer_1_out0[10], demultiplexer_1_out0[11], demultiplexer_1_out0[12], demultiplexer_1_out0[13], demultiplexer_1_out0[14], demultiplexer_1_out0[15]);
  Multiplexer #(.width(8)) multiplexer_1 (.in0(point_out), .in1({GG_out, 1'b0}), .out(multiplexer_1_out), .sel(in_2));
  or C (point_out[5], demultiplexer_1_out0[0], demultiplexer_1_out0[1], demultiplexer_1_out0[3], demultiplexer_1_out0[4], demultiplexer_1_out0[5], demultiplexer_1_out0[6], demultiplexer_1_out0[7], demultiplexer_1_out0[8], demultiplexer_1_out0[9]);
  or D (point_out[4], demultiplexer_1_out0[0], demultiplexer_1_out0[2], demultiplexer_1_out0[3], demultiplexer_1_out0[5], demultiplexer_1_out0[6], demultiplexer_1_out0[8], demultiplexer_1_out0[9]);
  _7_Segment_Display u_7_segment_display_1 (
    .g(multiplexer_1_out[1]), .f(multiplexer_1_out[2]), .a(multiplexer_1_out[7]), .b(multiplexer_1_out[6]),
    .e(multiplexer_1_out[3]), .d(multiplexer_1_out[4]), .c(multiplexer_1_out[5]), .dp(multiplexer_1_out[0]));
  or E (point_out[3], demultiplexer_1_out0[0], demultiplexer_1_out0[2], demultiplexer_1_out0[6], demultiplexer_1_out0[8]);
  or AA (GG_out[7], demultiplexer_1_out0[15], demultiplexer_1_out0[14], demultiplexer_1_out0[12], demultiplexer_1_out0[10], demultiplexer_1_out0[9], demultiplexer_1_out0[8], demultiplexer_1_out0[7], demultiplexer_1_out0[6], demultiplexer_1_out0[5], demultiplexer_1_out0[3], demultiplexer_1_out0[2], demultiplexer_1_out0[0]);
  or BB (GG_out[6], demultiplexer_1_out0[13], demultiplexer_1_out0[10], demultiplexer_1_out0[9], demultiplexer_1_out0[8], demultiplexer_1_out0[7], demultiplexer_1_out0[4], demultiplexer_1_out0[3], demultiplexer_1_out0[2], demultiplexer_1_out0[1], demultiplexer_1_out0[0]);
  or CC (GG_out[5], demultiplexer_1_out0[13], demultiplexer_1_out0[11], demultiplexer_1_out0[10], demultiplexer_1_out0[9], demultiplexer_1_out0[8], demultiplexer_1_out0[7], demultiplexer_1_out0[6], demultiplexer_1_out0[5], demultiplexer_1_out0[4], demultiplexer_1_out0[3], demultiplexer_1_out0[1], demultiplexer_1_out0[0]);
  or DD (GG_out[4], demultiplexer_1_out0[14], demultiplexer_1_out0[13], demultiplexer_1_out0[12], demultiplexer_1_out0[11], demultiplexer_1_out0[9], demultiplexer_1_out0[8], demultiplexer_1_out0[6], demultiplexer_1_out0[5], demultiplexer_1_out0[3], demultiplexer_1_out0[2], demultiplexer_1_out0[0]);
  or EE (GG_out[3], demultiplexer_1_out0[15], demultiplexer_1_out0[14], demultiplexer_1_out0[13], demultiplexer_1_out0[12], demultiplexer_1_out0[11], demultiplexer_1_out0[10], demultiplexer_1_out0[8], demultiplexer_1_out0[6], demultiplexer_1_out0[2], demultiplexer_1_out0[0]);
  or FF (GG_out[2], demultiplexer_1_out0[15], demultiplexer_1_out0[14], demultiplexer_1_out0[12], demultiplexer_1_out0[11], demultiplexer_1_out0[10], demultiplexer_1_out0[9], demultiplexer_1_out0[8], demultiplexer_1_out0[6], demultiplexer_1_out0[5], demultiplexer_1_out0[4], demultiplexer_1_out0[0]);
  or GG (GG_out[1], demultiplexer_1_out0[15], demultiplexer_1_out0[14], demultiplexer_1_out0[13], demultiplexer_1_out0[11], demultiplexer_1_out0[10], demultiplexer_1_out0[9], demultiplexer_1_out0[8], demultiplexer_1_out0[6], demultiplexer_1_out0[5], demultiplexer_1_out0[4], demultiplexer_1_out0[3], demultiplexer_1_out0[2]);
endmodule

module comparator4 (
  input  [3:0] in_1,
  input  [3:0] in_2,
  output out_3
);

  wire xnor_1_out, xnor_2_out, xnor_3_out, xnor_4_out;

  xnor xnor_1 (xnor_1_out, in_1[0], in_2[0]);
  xnor xnor_2 (xnor_2_out, in_1[1], in_2[1]);
  xnor xnor_3 (xnor_3_out, in_1[2], in_2[2]);
  xnor xnor_4 (xnor_4_out, in_1[3], in_2[3]);
  and and_1 (out_3, xnor_1_out, xnor_2_out, xnor_3_out, xnor_4_out);
endmodule

module fullAdder (
  input  A,
  input  B,
  input  Cin,
  output Y,
  output Cout
);

  wire nand_1_out, nand_2_out, nand_3_out, nand_4_out, nand_5_out, nand_6_out, nand_7_out, nand_8_out,
       not_1_out, not_2_out, not_3_out;

  not not_1 (not_1_out, A);
  not not_2 (not_2_out, B);
  not not_3 (not_3_out, Cin);
  nand nand_1 (nand_1_out, A, B, Cin);
  nand nand_2 (nand_2_out, not_3_out, not_2_out, A);
  nand nand_3 (nand_3_out, not_3_out, B, not_1_out);
  nand nand_4 (nand_4_out, Cin, not_2_out, not_1_out);
  nand nand_5 (nand_5_out, Cin, B, A);
  nand nand_6 (nand_6_out, not_3_out, B, A);
  nand nand_7 (nand_7_out, Cin, not_2_out, A);
  nand nand_8 (nand_8_out, Cin, B, not_1_out);
  nand nand_9 (Y, nand_1_out, nand_2_out, nand_3_out, nand_4_out);
  nand nand_10 (Cout, nand_5_out, nand_6_out, nand_7_out, nand_8_out);
endmodule

module halfAdder (
  input  A,
  input  B,
  output Y,
  output Cout
);

  xor xor_1 (Y, A, B);
  and and_1 (Cout, A, B);
endmodule

module adder_halfmade (
  input  in_1,
  input  in_2,
  input  in_3,
  output Y,
  output Cout
);

  wire halfadder_1_cout, halfadder_1_y, halfadder_2_cout;

  halfAdder halfadder_1 (.A(in_1), .B(in_2), .Y(halfadder_1_y), .Cout(halfadder_1_cout));
  halfAdder halfadder_2 (.A(halfadder_1_y), .B(in_3), .Y(Y), .Cout(halfadder_2_cout));
  or or_1 (Cout, halfadder_2_cout, halfadder_1_cout);
endmodule

module fullAdder4 (
  input  [3:0] A,
  input  [3:0] B,
  input  C0,
  output [3:0] Y,
  output Cout
);

  wire fulladder_1_cout, fulladder_2_cout, fulladder_3_cout;

  Hex_Digit_Display hex_digit_display_1 (.value(A));  // open: dp
  Hex_Digit_Display hex_digit_display_2 (.value(B));  // open: dp
  Hex_Digit_Display hex_digit_display_3 (.value(Y));  // open: dp
  LED led_1 (.in(Cout));
  fullAdder fulladder_1 (.A(A[0]), .B(B[0]), .Cin(C0), .Y(Y[0]), .Cout(fulladder_1_cout));
  fullAdder fulladder_2 (.A(A[1]), .B(B[1]), .Cin(fulladder_1_cout), .Y(Y[1]), .Cout(fulladder_2_cout));
  fullAdder fulladder_3 (.A(A[2]), .B(B[2]), .Cin(fulladder_2_cout), .Y(Y[2]), .Cout(fulladder_3_cout));
  fullAdder fulladder_4 (.A(A[3]), .B(B[3]), .Cin(fulladder_3_cout), .Y(Y[3]), .Cout(Cout));

  // Notes on the sheet:
  //   +
  //   =
endmodule

module fullSubtractor (
  input  A,
  input  B,
  input  Bin,
  output D,
  output Bout
);

  wire nand_1_out, nand_2_out, nand_3_out, nand_4_out, nand_5_out, nand_6_out, nand_7_out, nand_8_out,
       not_1_out, not_2_out, not_3_out;

  not not_1 (not_1_out, A);
  not not_2 (not_2_out, B);
  not not_3 (not_3_out, Bin);
  nand nand_1 (nand_1_out, A, B, Bin);
  nand nand_2 (nand_2_out, not_3_out, not_2_out, A);
  nand nand_3 (nand_3_out, not_3_out, B, not_1_out);
  nand nand_4 (nand_4_out, Bin, not_2_out, not_1_out);
  nand nand_5 (nand_5_out, A, B, Bin);
  nand nand_6 (nand_6_out, not_1_out, B, Bin);
  nand nand_7 (nand_7_out, not_1_out, B, not_3_out);
  nand nand_8 (nand_8_out, Bin, not_2_out, not_1_out);
  nand nand_9 (D, nand_1_out, nand_2_out, nand_3_out, nand_4_out);
  nand nand_10 (Bout, nand_5_out, nand_6_out, nand_7_out, nand_8_out);
endmodule

module fullSubstractor4 (
  input  [3:0] A,
  input  [3:0] B,
  input  C0,
  output sign,
  output [3:0] D
);

  wire fullsubtractor_1_bout, fullsubtractor_2_bout, fullsubtractor_3_bout;
  wire [3:0] adder_1_out, fullsubtractor_1_d, not_1_out;

  Hex_Digit_Display hex_digit_display_1 (.value(A));  // open: dp
  Hex_Digit_Display hex_digit_display_2 (.value(B));  // open: dp
  _7_Segment_Display u_7_segment_display_1 (.g(sign));  // open: f, a, b, e, d, c, dp
  Hex_Digit_Display hex_digit_display_3 (.value(D));  // open: dp
  fullSubtractor fullsubtractor_1 (
    .A(A[0]), .B(B[0]), .Bin(C0), .D(fullsubtractor_1_d[0]), .Bout(fullsubtractor_1_bout));
  fullSubtractor fullsubtractor_2 (
    .A(A[1]), .B(B[1]), .Bin(fullsubtractor_1_bout), .D(fullsubtractor_1_d[1]), .Bout(fullsubtractor_2_bout));
  fullSubtractor fullsubtractor_3 (
    .A(A[2]), .B(B[2]), .Bin(fullsubtractor_2_bout), .D(fullsubtractor_1_d[2]), .Bout(fullsubtractor_3_bout));
  fullSubtractor fullsubtractor_4 (
    .A(A[3]), .B(B[3]), .Bin(fullsubtractor_3_bout), .D(fullsubtractor_1_d[3]), .Bout(sign));
  assign not_1_out = ~fullsubtractor_1_d;  // NOT_Gate not_1, 4 bits wide
  Adder #(.width(4)) adder_1 (.a(not_1_out), .b(4'b0001), .out(adder_1_out));  // open: cin, cout
  Multiplexer #(.width(4)) multiplexer_1 (.in0(fullsubtractor_1_d), .in1(adder_1_out), .out(D), .sel(sign));

  // Notes on the sheet:
  //   -
  //   =
endmodule

module signMagnitudeAdder5 (
  input  [4:0] A,
  input  [4:0] B
);

  wire fullsubstractor4_1_sign, multiplexer_1_out, xnor_1_out;
  wire [3:0] adder_1_out, fullsubstractor4_1_d, multiplexer_2_out;

  _7_Segment_Display u_7_segment_display_1 (.g(A[4]));  // open: f, a, b, e, d, c, dp
  Hex_Digit_Display hex_digit_display_1 (.value(A[3:0]));  // open: dp
  _7_Segment_Display u_7_segment_display_2 (.g(B[4]));  // open: f, a, b, e, d, c, dp
  Adder #(.width(4)) adder_1 (.a(A[3:0]), .b(B[3:0]), .out(adder_1_out));  // open: cin, cout
  xnor xnor_1 (xnor_1_out, A[4], B[4]);
  Multiplexer multiplexer_1 (.in0(A[4]), .in1(B[4]), .out(multiplexer_1_out), .sel(fullsubstractor4_1_sign));
  Hex_Digit_Display hex_digit_display_2 (.value(B[3:0]));  // open: dp
  _7_Segment_Display u_7_segment_display_3 (.g(multiplexer_1_out));  // open: f, a, b, e, d, c, dp
  Hex_Digit_Display hex_digit_display_3 (.value(multiplexer_2_out));  // open: dp
  fullSubstractor4 fullsubstractor4_1 (
    .A(A[3:0]), .B(B[3:0]), .sign(fullsubstractor4_1_sign), .D(fullsubstractor4_1_d));  // open: C0
  Multiplexer #(.width(4)) multiplexer_2 (
    .in0(fullsubstractor4_1_d), .in1(adder_1_out), .out(multiplexer_2_out), .sel(xnor_1_out));

  // Notes on the sheet:
  //   +
  //   =
endmodule

module onesComplementAdder (
  input  [3:0] A,
  input  [3:0] B,
  output [3:0] Y,
  output V
);

  wire [2:0] multiplexer_1_out, multiplexer_2_out, not_1_out, not_2_out, not_3_out, signmagnitudeadder4_1_y;

  onesComplementAdder2 onescomplementadder2_1 ();  // open: A, B, out_3
  assign not_1_out = ~A[2:0];  // NOT_Gate not_1, 3 bits wide
  assign not_2_out = ~B[2:0];  // NOT_Gate not_2, 3 bits wide
  Multiplexer #(.width(3)) multiplexer_1 (.in0(A[2:0]), .in1(not_1_out), .out(multiplexer_1_out), .sel(A[3]));
  Multiplexer #(.width(3)) multiplexer_2 (.in0(B[2:0]), .in1(not_2_out), .out(multiplexer_2_out), .sel(B[3]));
  signMagnitudeAdder4 signmagnitudeadder4_1 (
    .A({A[3], multiplexer_1_out}), .B({B[3], multiplexer_2_out}), .Y({Y[3], signmagnitudeadder4_1_y}), .V(V));
  LED led_1 (.in(V));
  assign not_3_out = ~signmagnitudeadder4_1_y;  // NOT_Gate not_3, 3 bits wide
  Multiplexer #(.width(3)) multiplexer_3 (.in0(signmagnitudeadder4_1_y), .in1(not_3_out), .out(Y[2:0]), .sel(Y[3]));

  // Notes on the sheet:
  //   反码转原码
  //   4位原码加法器
  //   原码转反码
endmodule

module signMagnitudeAdder4 (
  input  [3:0] A,
  input  [3:0] B,
  output [3:0] Y,
  output V
);

  wire fullsubstractor4_1_sign, xnor_1_out;
  wire [3:0] adder_1_out, fullsubstractor4_1_d;

  _7_Segment_Display u_7_segment_display_1 (.g(A[3]));  // open: f, a, b, e, d, c, dp
  Hex_Digit_Display hex_digit_display_1 (.value({1'b0, A[2:0]}));  // open: dp
  _7_Segment_Display u_7_segment_display_2 (.g(B[3]));  // open: f, a, b, e, d, c, dp
  Adder #(.width(4)) adder_1 (.a({1'b0, A[2:0]}), .b({1'b0, B[2:0]}), .out(adder_1_out));  // open: cin, cout
  xnor xnor_1 (xnor_1_out, A[3], B[3]);
  Hex_Digit_Display hex_digit_display_2 (.value({1'b0, B[2:0]}));  // open: dp
  Multiplexer multiplexer_1 (.in0(A[3]), .in1(B[3]), .out(Y[3]), .sel(fullsubstractor4_1_sign));
  fullSubstractor4 fullsubstractor4_1 (
    .A({1'b0, A[2:0]}), .B({1'b0, B[2:0]}), .sign(fullsubstractor4_1_sign), .D(fullsubstractor4_1_d));  // open: C0
  _7_Segment_Display u_7_segment_display_3 (.g(Y[3]));  // open: f, a, b, e, d, c, dp
  Hex_Digit_Display hex_digit_display_3 (.value({V, Y[2:0]}));  // open: dp
  Multiplexer #(.width(4)) multiplexer_2 (
    .in0(fullsubstractor4_1_d), .in1(adder_1_out), .out({V, Y[2:0]}), .sel(xnor_1_out));

  // Notes on the sheet:
  //   +
  //   =
  //   A>B时，sign总指向A
  //   A<B时，sign总指向B
endmodule

module onesComplementAdder2 (
  input  [3:0] A,
  input  [3:0] B,
  output [3:0] out_3
);

  wire fulladder4_1_cout;

  fullAdder4 fulladder4_1 (.A(A), .B(B), .C0(fulladder4_1_cout), .Y(out_3), .Cout(fulladder4_1_cout));
endmodule

module SRLatch (
  input  S,
  input  R,
  output Q,
  output Q_f
);

  nor nor_1 (Q, R, Q_f);
  nor nor_2 (Q_f, Q, S);
endmodule

module DLatch (
  input  WE,
  input  D,
  input  R,
  output Q,
  output Q_f
);

  wire and_1_out, and_2_out, and_3_out, not_1_out, not_2_out, or_1_out;

  not not_1 (not_1_out, D);
  and and_1 (and_1_out, D, WE);
  and and_2 (and_2_out, WE, not_1_out);
  and and_3 (and_3_out, and_1_out, not_2_out);
  not not_2 (not_2_out, R);
  or or_1 (or_1_out, and_2_out, R);
  SRLatch srlatch_1 (.S(and_3_out), .R(or_1_out), .Q(Q), .Q_f(Q_f));
endmodule

module DFlipFlop (
  input  D,
  input  WE,
  input  CLK,
  input  R,
  output Q,
  output Q_f
);

  wire and_1_out, and_2_out, dlatch_1_q, not_1_out;

  not not_1 (not_1_out, and_2_out);
  and and_1 (and_1_out, D, WE);
  and and_2 (and_2_out, WE, CLK);
  DLatch dlatch_1 (.WE(not_1_out), .D(and_1_out), .R(R), .Q(dlatch_1_q));  // open: Q_f
  DLatch dlatch_2 (.WE(and_2_out), .D(dlatch_1_q), .R(R), .Q(Q), .Q_f(Q_f));
endmodule

module DflipflopDownControl (
  input  CLK,
  input  D,
  input  R,
  output Q,
  output Q_f
);

  wire dlatch_1_q, not_1_out;

  not not_1 (not_1_out, CLK);
  DLatch dlatch_1 (.WE(CLK), .D(D), .R(R), .Q(dlatch_1_q));  // open: Q_f
  DLatch dlatch_2 (.WE(not_1_out), .D(dlatch_1_q), .R(R), .Q(Q), .Q_f(Q_f));
endmodule

module DRegister (
  input  [3:0] D,
  input  WE,
  input  CLK,
  input  R,
  output out_5,
  output out_6,
  output out_7,
  output out_8
);

  DFlipFlop dflipflop_1 (.D(D[0]), .WE(WE), .CLK(CLK), .R(R), .Q(out_5));  // open: Q_f
  DFlipFlop dflipflop_2 (.D(D[1]), .WE(WE), .CLK(CLK), .R(R), .Q(out_6));  // open: Q_f
  DFlipFlop dflipflop_3 (.D(D[2]), .WE(WE), .CLK(CLK), .R(R), .Q(out_7));  // open: Q_f
  DFlipFlop dflipflop_4 (.D(D[3]), .WE(WE), .CLK(CLK), .R(R), .Q(out_8));  // open: Q_f
  Hex_Digit_Display hex_digit_display_1 (.value({out_8, out_7, out_6, out_5}));  // open: dp
endmodule

module counter4Bit (
  input  WE,
  input  CLK,
  input  R,
  output [3:0] Y,
  output Cout
);

  wire [3:0] fulladder4_1_y;

  DFlipFlop dflipflop_1 (.D(fulladder4_1_y[0]), .WE(WE), .CLK(CLK), .R(R), .Q(Y[0]));  // open: Q_f
  DFlipFlop dflipflop_2 (.D(fulladder4_1_y[1]), .WE(WE), .CLK(CLK), .R(R), .Q(Y[1]));  // open: Q_f
  DFlipFlop dflipflop_3 (.D(fulladder4_1_y[2]), .WE(WE), .CLK(CLK), .R(R), .Q(Y[2]));  // open: Q_f
  DFlipFlop dflipflop_4 (.D(fulladder4_1_y[3]), .WE(WE), .CLK(CLK), .R(R), .Q(Y[3]));  // open: Q_f
  Hex_Digit_Display hex_digit_display_1 (.value(Y));  // open: dp
  fullAdder4 fulladder4_1 (.A(Y), .B(4'b0001), .Y(fulladder4_1_y), .Cout(Cout));  // open: C0
endmodule

module DRegister8 (
  input  [7:0] D,
  input  WE,
  input  CLK,
  input  R,
  output [7:0] Y
);

  DFlipFlop dflipflop_1 (.D(D[0]), .WE(WE), .CLK(CLK), .R(R), .Q(Y[0]));  // open: Q_f
  DFlipFlop dflipflop_2 (.D(D[1]), .WE(WE), .CLK(CLK), .R(R), .Q(Y[1]));  // open: Q_f
  DFlipFlop dflipflop_3 (.D(D[2]), .WE(WE), .CLK(CLK), .R(R), .Q(Y[2]));  // open: Q_f
  DFlipFlop dflipflop_4 (.D(D[3]), .WE(WE), .CLK(CLK), .R(R), .Q(Y[3]));  // open: Q_f
  DFlipFlop dflipflop_5 (.D(D[4]), .WE(WE), .CLK(CLK), .R(R), .Q(Y[4]));  // open: Q_f
  DFlipFlop dflipflop_6 (.D(D[5]), .WE(WE), .CLK(CLK), .R(R), .Q(Y[5]));  // open: Q_f
  DFlipFlop dflipflop_7 (.D(D[6]), .WE(WE), .CLK(CLK), .R(R), .Q(Y[6]));  // open: Q_f
  DFlipFlop dflipflop_8 (.D(D[7]), .WE(WE), .CLK(CLK), .R(R), .Q(Y[7]));  // open: Q_f
endmodule

module adder8 (
  input  Cin,
  input  [7:0] A,
  input  [7:0] B,
  output [7:0] Y,
  output Cout
);

  wire fulladder4_1_cout;

  fullAdder4 fulladder4_1 (.A(A[3:0]), .B(B[3:0]), .C0(Cin), .Y(Y[3:0]), .Cout(fulladder4_1_cout));
  fullAdder4 fulladder4_2 (.A(A[7:4]), .B(B[7:4]), .C0(fulladder4_1_cout), .Y(Y[7:4]), .Cout(Cout));
endmodule

module Accumulator8Bit (
  input  in_1,
  input  in_2,
  input  in_3,
  output [7:0] out_4
);

  wire [7:0] adder8_1_y, dregister8_1_y, dregister8_2_y;

  DRegister8 dregister8_1 (.D(adder8_1_y), .WE(in_1), .CLK(in_2), .R(in_3), .Y(dregister8_1_y));
  DRegister8 dregister8_2 (.D(out_4), .WE(in_1), .CLK(in_2), .R(in_3), .Y(dregister8_2_y));
  adder8 adder8_1 (.A(dregister8_1_y), .B(8'h1), .Y(adder8_1_y));  // open: Cin, Cout
  adder8 adder8_2 (.A(adder8_1_y), .B(dregister8_2_y), .Y(out_4));  // open: Cin, Cout
endmodule

module aClock (
  input  WE,
  input  R
);

  wire CLK_out, comparator4_1_out_3, comparator4_2_out_3, comparator4_3_out_3, comparator4_4_out_3, or_1_out,
       or_2_out, or_3_out, or_4_out;
  wire [3:0] counter4bit_1_y, counter4bit_2_y, counter4bit_3_y, counter4bit_4_y;

  Clock CLK (.out(CLK_out));
  or or_1 (or_1_out, R, comparator4_1_out_3);
  or or_2 (or_2_out, R, comparator4_2_out_3);
  or or_3 (or_3_out, R, comparator4_3_out_3);
  or or_4 (or_4_out, R, comparator4_4_out_3);
  Hex_Digit_Display hex_digit_display_1 (.value(counter4bit_4_y));  // open: dp
  Hex_Digit_Display hex_digit_display_2 (.value(counter4bit_3_y));  // open: dp
  counter4Bit counter4bit_1 (.WE(WE), .CLK(CLK_out), .R(or_1_out), .Y(counter4bit_1_y));  // open: Cout
  counter4Bit counter4bit_2 (.WE(WE), .CLK(comparator4_1_out_3), .R(or_2_out), .Y(counter4bit_2_y));  // open: Cout
  counter4Bit counter4bit_3 (.WE(WE), .CLK(comparator4_2_out_3), .R(or_3_out), .Y(counter4bit_3_y));  // open: Cout
  counter4Bit counter4bit_4 (.WE(WE), .CLK(comparator4_3_out_3), .R(or_4_out), .Y(counter4bit_4_y));  // open: Cout
  Hex_Digit_Display hex_digit_display_3 (.value(counter4bit_2_y));  // open: dp
  Hex_Digit_Display hex_digit_display_4 (.value(counter4bit_1_y));  // open: dp
  comparator4 comparator4_1 (.in_1(counter4bit_1_y), .in_2(4'b1010), .out_3(comparator4_1_out_3));
  comparator4 comparator4_2 (.in_1(counter4bit_2_y), .in_2(4'b0110), .out_3(comparator4_2_out_3));
  comparator4 comparator4_3 (.in_1(counter4bit_3_y), .in_2(4'b1010), .out_3(comparator4_3_out_3));
  comparator4 comparator4_4 (.in_1(counter4bit_4_y), .in_2(4'b0110), .out_3(comparator4_4_out_3));

  // Notes on the sheet:
  //   :
endmodule

module aClock2 (
  input  WE,
  input  R
);

  wire CLK_out, comparator4_1_out_3, comparator4_2_out_3, comparator4_3_out_3, comparator4_4_out_3, or_1_out,
       or_2_out, or_3_out, or_4_out;
  wire [3:0] counter4bit_1_y, counter4bit_2_y, counter4bit_3_y, counter4bit_4_y;

  Clock CLK (.out(CLK_out));
  or or_1 (or_1_out, R, comparator4_1_out_3);
  or or_2 (or_2_out, R, comparator4_2_out_3);
  or or_3 (or_3_out, R, comparator4_3_out_3);
  or or_4 (or_4_out, R, comparator4_4_out_3);
  Hex_Digit_Display hex_digit_display_1 (.value(counter4bit_4_y));  // open: dp
  Hex_Digit_Display hex_digit_display_2 (.value(counter4bit_3_y));  // open: dp
  counter4Bit counter4bit_1 (.WE(WE), .CLK(CLK_out), .R(or_1_out), .Y(counter4bit_1_y));  // open: Cout
  counter4Bit counter4bit_2 (.WE(comparator4_1_out_3), .CLK(CLK_out), .R(or_2_out), .Y(counter4bit_2_y));  // open: Cout
  counter4Bit counter4bit_3 (.WE(comparator4_2_out_3), .CLK(CLK_out), .R(or_3_out), .Y(counter4bit_3_y));  // open: Cout
  counter4Bit counter4bit_4 (.WE(comparator4_3_out_3), .CLK(CLK_out), .R(or_4_out), .Y(counter4bit_4_y));  // open: Cout
  Hex_Digit_Display hex_digit_display_3 (.value(counter4bit_2_y));  // open: dp
  Hex_Digit_Display hex_digit_display_4 (.value(counter4bit_1_y));  // open: dp
  comparator4 comparator4_1 (.in_1(counter4bit_1_y), .in_2(4'b1010), .out_3(comparator4_1_out_3));
  comparator4 comparator4_2 (.in_1(counter4bit_2_y), .in_2(4'b0110), .out_3(comparator4_2_out_3));
  comparator4 comparator4_3 (.in_1(counter4bit_3_y), .in_2(4'b1010), .out_3(comparator4_3_out_3));
  comparator4 comparator4_4 (.in_1(counter4bit_4_y), .in_2(4'b0110), .out_3(comparator4_4_out_3));

  // Notes on the sheet:
  //   TODO: 修改外部电路对抗脉冲信号
  //   排查问题：SR锁存器获得1刻钟S1R0信号并回到S0R0锁存后，SR锁存器将陷入00 11震荡
  //   :
endmodule
