// Logisim project minirv.circ as structural Verilog: 11 circuits, main circuit main
module main (
);

  wire clock_1_out, comparator_1_eq, comparator_2_eq, comparator_3_eq, comparator_4_eq, comparator_5_eq,
       comparator_6_eq, comparator_7_eq, comparator_8_eq, or_1_out, or_2_out, sb_1_byte_select;
  wire [1:0] pc_1_y;
  wire [3:0] bit_extender_1_out, bit_extender_2_out, bit_extender_3_out, multiplexer_1_out, sb_1_byte_addr;
  wire [9:0] rom_1_data_2;
  wire [16:0] lw_1_memory_addr, pc_1_y_2;
  wire [18:0] jalr_1_destination_addr;
  wire [31:0] addi_1_rd_data, gpr_1_data1, gpr_1_data2, ram_1_dout, sw_1_memory_data;
  wire [31:7] rom_1_data;

  Clock clock_1 (.out(clock_1_out));
  Counter #(.max('hffffffffffffffff), .width(64)) counter_1 (.clk(clock_1_out));  // open: clr, load, up, count, D, carry, Q
  ROM #(.addrWidth(17), .dataWidth(32)) rom_1 (
    .addr(pc_1_y_2), .data({rom_1_data[31:15], rom_1_data_2[9:7], rom_1_data[11:7], rom_1_data_2[6:0]}));
  PC pc_1 (.CLK(clock_1_out), .ADDR(jalr_1_destination_addr), .EN(comparator_2_eq), .Y({pc_1_y_2, pc_1_y}));
  Bit_Extender #(.in_width(5), .out_width(4), .\type ("zero")) bit_extender_1 (
    .in(rom_1_data[11:7]), .out(bit_extender_1_out));
  Bit_Extender #(.in_width(5), .out_width(4), .\type ("zero")) bit_extender_2 (
    .in(rom_1_data[19:15]), .out(bit_extender_2_out));
  Bit_Extender #(.in_width(5), .out_width(4), .\type ("zero")) bit_extender_3 (
    .in(rom_1_data[24:20]), .out(bit_extender_3_out));
  Comparator #(.width(7)) comparator_1 (.a(7'b0010011), .b(rom_1_data_2[6:0]), .eq(comparator_1_eq));  // open: gt, lt
  Comparator #(.width(7)) comparator_2 (.a(7'b1100111), .b(rom_1_data_2[6:0]), .eq(comparator_2_eq));  // open: gt, lt
  Comparator #(.width(7)) comparator_3 (.a(7'b0110011), .b(rom_1_data_2[6:0]), .eq(comparator_3_eq));  // open: gt, lt
  Comparator #(.width(7)) comparator_4 (.a(7'b0110111), .b(rom_1_data_2[6:0]), .eq(comparator_4_eq));  // open: gt, lt
  Comparator #(.width(10)) comparator_5 (.a(10'h103), .b(rom_1_data_2), .eq(comparator_5_eq));  // open: gt, lt
  Comparator #(.width(10)) comparator_6 (.a(10'h123), .b(rom_1_data_2), .eq(comparator_6_eq));  // open: gt, lt
  Comparator #(.width(10)) comparator_7 (.a(10'h203), .b(rom_1_data_2), .eq(comparator_7_eq));  // open: gt, lt
  Comparator #(.width(10)) comparator_8 (.a(10'h23), .b(rom_1_data_2), .eq(comparator_8_eq));  // open: gt, lt
  or or_1 (or_1_out, comparator_5_eq, comparator_1_eq, comparator_2_eq, comparator_3_eq, comparator_4_eq, comparator_7_eq);
  or or_2 (or_2_out, comparator_6_eq, comparator_8_eq);
  GPR gpr_1 (
    .clk(clock_1_out), .wdata(addi_1_rd_data), .wadds(bit_extender_1_out), .wen(or_1_out),
    .radds1(bit_extender_2_out), .radds2(bit_extender_3_out), .data1(gpr_1_data1), .data2(gpr_1_data2));
  ADDI addi_1 (.en(comparator_1_eq), .rs_data(gpr_1_data1), .imm(rom_1_data[31:20]), .rd_data(addi_1_rd_data));
  JALR jalr_1 (
    .en(comparator_2_eq), .rs1(gpr_1_data1), .imm(rom_1_data[31:20]), .PC_addr({pc_1_y_2, pc_1_y}),
    .destination_addr(jalr_1_destination_addr), .return_PC(addi_1_rd_data));
  ADD add_1 (.en(comparator_3_eq), .rs1_data(gpr_1_data1), .rs2_data(gpr_1_data2), .rd_data(addi_1_rd_data));
  LUI lui_1 (.en(comparator_4_eq), .imm_data({rom_1_data[31:15], rom_1_data_2[9:7]}), .rd_data(addi_1_rd_data));
  LW lw_1 (
    .en(comparator_5_eq), .rs_data(gpr_1_data1), .offset(rom_1_data[31:20]), .memory_data(ram_1_dout),
    .memory_addr(lw_1_memory_addr), .rd_data(addi_1_rd_data));
  SW sw_1 (
    .en(comparator_6_eq), .rs1_data(gpr_1_data1), .offset({rom_1_data[31:25], rom_1_data[11:7]}),
    .rs2_data(gpr_1_data2), .memory_addr(lw_1_memory_addr), .memory_data(sw_1_memory_data));
  LBU lbu_1 (
    .en(comparator_7_eq), .rs_data(gpr_1_data1), .offset(rom_1_data[31:20]), .memory_data(ram_1_dout),
    .memory_addr(lw_1_memory_addr), .rd_data(addi_1_rd_data));
  SB sb_1 (
    .en(comparator_8_eq), .rs1_data(gpr_1_data1), .offset({rom_1_data[31:25], rom_1_data[11:7]}),
    .rs2_data(gpr_1_data2), .byte_addr(sb_1_byte_addr), .memory_addr(lw_1_memory_addr),
    .memory_data(sw_1_memory_data), .byte_select(sb_1_byte_select));
  RAM #(.addrWidth(17), .asyncread("true"), .byteenables("byteEnables"), .dataWidth(32), .\type ("nonvolatile")) ram_1 (
    .addr(lw_1_memory_addr), .we(or_2_out), .oe(1'b1), .clk(clock_1_out), .din(sw_1_memory_data),
    .dout(ram_1_dout), .be3(multiplexer_1_out[0]), .be2(multiplexer_1_out[1]), .be1(multiplexer_1_out[2]),
    .be0(multiplexer_1_out[3]));
  Multiplexer #(.width(4)) multiplexer_1 (
    .in0(4'b1111), .in1(sb_1_byte_addr), .out(multiplexer_1_out), .sel(sb_1_byte_select));

  // Notes on the sheet:
  //   contents of rom_1 (hex, n*v repeats v):
  //   87654137 32110113 202823 1004183 1104203 1204283 1304303 2a23 600a23 400b23 1402383 4000413 400e7
  //   748533 a02c23 ffc40067 5184b3 8067
  //   opcode
  //   funct3
  //   I type
  //   U type
  //   S type
  //   rd
  //   rs1
  //   rs2
  //   ADDI
  //   JALR
  //   ADD
  //   LUI
  //   LW
  //   SW
  //   LBU
  //   SB
endmodule

module GPR (
  input  clk,
  input  [31:0] wdata,
  input  [3:0] wadds,
  input  wen,
  input  [3:0] radds1,
  input  [3:0] radds2,
  output [31:0] data1,
  output [31:0] data2
);

  wire decoder_1_out1, decoder_1_out2, decoder_1_out3, decoder_1_out4, decoder_1_out5, decoder_1_out6,
       decoder_1_out7, decoder_1_out8, decoder_1_out9, decoder_1_out10, decoder_1_out11, decoder_1_out12,
       decoder_1_out13, decoder_1_out14, decoder_1_out15;
  wire [31:0] register_1_q, register_2_q, register_3_q, register_4_q, register_5_q, register_6_q,
       register_7_q, register_8_q, register_9_q, register_10_q, register_11_q, register_12_q, register_13_q,
       register_14_q, register_15_q;

  Decoder #(.select(4)) decoder_1 (
    .out1(decoder_1_out1), .out2(decoder_1_out2), .out3(decoder_1_out3), .out4(decoder_1_out4),
    .out5(decoder_1_out5), .out6(decoder_1_out6), .out7(decoder_1_out7), .out8(decoder_1_out8),
    .out9(decoder_1_out9), .out10(decoder_1_out10), .out11(decoder_1_out11), .out12(decoder_1_out12),
    .out13(decoder_1_out13), .out14(decoder_1_out14), .out15(decoder_1_out15), .sel(wadds), .en(wen));  // open: out0
  Register #(.width(32)) register_1 (.D(wdata), .en(decoder_1_out8), .clk(clk), .Q(register_1_q));  // open: clr
  Register #(.width(32)) register_2 (.D(wdata), .en(decoder_1_out1), .clk(clk), .Q(register_2_q));  // open: clr
  Register #(.width(32)) register_3 (.D(wdata), .en(decoder_1_out9), .clk(clk), .Q(register_3_q));  // open: clr
  Register #(.width(32)) register_4 (.D(wdata), .en(decoder_1_out2), .clk(clk), .Q(register_4_q));  // open: clr
  Register #(.width(32)) register_5 (.D(wdata), .en(decoder_1_out10), .clk(clk), .Q(register_5_q));  // open: clr
  Register #(.width(32)) register_6 (.D(wdata), .en(decoder_1_out3), .clk(clk), .Q(register_6_q));  // open: clr
  Register #(.width(32)) register_7 (.D(wdata), .en(decoder_1_out11), .clk(clk), .Q(register_7_q));  // open: clr
  Register #(.width(32)) register_8 (.D(wdata), .en(decoder_1_out4), .clk(clk), .Q(register_8_q));  // open: clr
  Register #(.width(32)) register_9 (.D(wdata), .en(decoder_1_out12), .clk(clk), .Q(register_9_q));  // open: clr
  Register #(.width(32)) register_10 (.D(wdata), .en(decoder_1_out5), .clk(clk), .Q(register_10_q));  // open: clr
  Register #(.width(32)) register_11 (.D(wdata), .en(decoder_1_out13), .clk(clk), .Q(register_11_q));  // open: clr
  Register #(.width(32)) register_12 (.D(wdata), .en(decoder_1_out6), .clk(clk), .Q(register_12_q));  // open: clr
  Register #(.width(32)) register_13 (.D(wdata), .en(decoder_1_out14), .clk(clk), .Q(register_13_q));  // open: clr
  Register #(.width(32)) register_14 (.D(wdata), .en(decoder_1_out7), .clk(clk), .Q(register_14_q));  // open: clr
  Register #(.width(32)) register_15 (.D(wdata), .en(decoder_1_out15), .clk(clk), .Q(register_15_q));  // open: clr
  Multiplexer #(.select(4), .width(32)) multiplexer_1 (
    .in0({32{1'b0}}), .in1(register_2_q), .in2(register_4_q), .in3(register_6_q), .in4(register_8_q),
    .in5(register_10_q), .in6(register_12_q), .in7(register_14_q), .in8(register_1_q), .in9(register_3_q),
    .in10(register_5_q), .in11(register_7_q), .in12(register_9_q), .in13(register_11_q),
    .in14(register_13_q), .in15(register_15_q), .out(data1), .sel(radds1));
  Multiplexer #(.select(4), .width(32)) multiplexer_2 (
    .in0({32{1'b0}}), .in1(register_2_q), .in2(register_4_q), .in3(register_6_q), .in4(register_8_q),
    .in5(register_10_q), .in6(register_12_q), .in7(register_14_q), .in8(register_1_q), .in9(register_3_q),
    .in10(register_5_q), .in11(register_7_q), .in12(register_9_q), .in13(register_11_q),
    .in14(register_13_q), .in15(register_15_q), .out(data2), .sel(radds2));
endmodule

module PC (
  input  CLK,
  input  [18:0] ADDR,
  input  EN,
  output [18:0] Y
);

  wire [18:0] adder_1_out, multiplexer_1_out;

  D_Flip_Flop d_ff_1 (.D(multiplexer_1_out[0]), .clk(CLK), .Q(Y[0]));  // open: Qn, preset, reset
  D_Flip_Flop d_ff_2 (.D(multiplexer_1_out[1]), .clk(CLK), .Q(Y[1]));  // open: Qn, preset, reset
  D_Flip_Flop d_ff_3 (.D(multiplexer_1_out[2]), .clk(CLK), .Q(Y[2]));  // open: Qn, preset, reset
  D_Flip_Flop d_ff_4 (.D(multiplexer_1_out[3]), .clk(CLK), .Q(Y[3]));  // open: Qn, preset, reset
  D_Flip_Flop d_ff_5 (.D(multiplexer_1_out[4]), .clk(CLK), .Q(Y[4]));  // open: Qn, preset, reset
  D_Flip_Flop d_ff_6 (.D(multiplexer_1_out[5]), .clk(CLK), .Q(Y[5]));  // open: Qn, preset, reset
  D_Flip_Flop d_ff_7 (.D(multiplexer_1_out[6]), .clk(CLK), .Q(Y[6]));  // open: Qn, preset, reset
  D_Flip_Flop d_ff_8 (.D(multiplexer_1_out[7]), .clk(CLK), .Q(Y[7]));  // open: Qn, preset, reset
  D_Flip_Flop d_ff_9 (.D(multiplexer_1_out[8]), .clk(CLK), .Q(Y[8]));  // open: Qn, preset, reset
  D_Flip_Flop d_ff_10 (.D(multiplexer_1_out[9]), .clk(CLK), .Q(Y[9]));  // open: Qn, preset, reset
  D_Flip_Flop d_ff_11 (.D(multiplexer_1_out[10]), .clk(CLK), .Q(Y[10]));  // open: Qn, preset, reset
  D_Flip_Flop d_ff_12 (.D(multiplexer_1_out[11]), .clk(CLK), .Q(Y[11]));  // open: Qn, preset, reset
  D_Flip_Flop d_ff_13 (.D(multiplexer_1_out[12]), .clk(CLK), .Q(Y[12]));  // open: Qn, preset, reset
  D_Flip_Flop d_ff_14 (.D(multiplexer_1_out[13]), .clk(CLK), .Q(Y[13]));  // open: Qn, preset, reset
  D_Flip_Flop d_ff_15 (.D(multiplexer_1_out[14]), .clk(CLK), .Q(Y[14]));  // open: Qn, preset, reset
  D_Flip_Flop d_ff_16 (.D(multiplexer_1_out[15]), .clk(CLK), .Q(Y[15]));  // open: Qn, preset, reset
  D_Flip_Flop d_ff_17 (.D(multiplexer_1_out[16]), .clk(CLK), .Q(Y[16]));  // open: Qn, preset, reset
  D_Flip_Flop d_ff_18 (.D(multiplexer_1_out[17]), .clk(CLK), .Q(Y[17]));  // open: Qn, preset, reset
  D_Flip_Flop d_ff_19 (.D(multiplexer_1_out[18]), .clk(CLK), .Q(Y[18]));  // open: Qn, preset, reset
  Adder #(.width(19)) adder_1 (.a(Y), .b(19'h4), .out(adder_1_out));  // open: cin, cout
  Multiplexer #(.width(19)) multiplexer_1 (.in0(adder_1_out), .in1(ADDR), .out(multiplexer_1_out), .sel(EN));
endmodule

module ADDI (
  input  en,
  input  [31:0] rs_data,
  input  [11:0] imm,
  output [31:0] rd_data
);

  wire [31:0] adder_1_out, bit_extender_1_out;

  assign bit_extender_1_out = {{20{imm[11]}}, imm};  // Bit_Extender bit_extender_1
  Adder #(.width(32)) adder_1 (.a(rs_data), .b(bit_extender_1_out), .out(adder_1_out));  // open: cin, cout
  assign rd_data = en ? adder_1_out : 32'bz;  // Controlled_Buffer controlled_buffer_1
endmodule

module JALR (
  input  en,
  input  [31:0] rs1,
  input  [11:0] imm,
  input  [18:0] PC_addr,
  output [18:0] destination_addr,
  output [31:0] return_PC
);

  wire [18:0] adder_1_out;
  wire [31:0] adder_2_out, bit_extender_1_out, bit_extender_2_out, controlled_buffer_1_out;

  assign bit_extender_1_out = {{20{1'b0}}, imm};  // Bit_Extender bit_extender_1
  Adder #(.width(19)) adder_1 (.a(PC_addr), .b(19'h4), .out(adder_1_out));  // open: cin, cout
  Adder #(.width(32)) adder_2 (.a(rs1), .b(bit_extender_1_out), .out(adder_2_out));  // open: cin, cout
  assign bit_extender_2_out = {{13{1'b0}}, adder_1_out};  // Bit_Extender bit_extender_2
  assign {controlled_buffer_1_out[31:19], destination_addr[18:2], controlled_buffer_1_out[1:0]} = en ? adder_2_out : 32'bz;  // Controlled_Buffer controlled_buffer_1
  assign return_PC = en ? bit_extender_2_out : 32'bz;  // Controlled_Buffer controlled_buffer_2

  assign destination_addr[1:0] = 2'b00;
endmodule

module ADD (
  input  en,
  input  [31:0] rs1_data,
  input  [31:0] rs2_data,
  output [31:0] rd_data
);

  wire [31:0] adder_1_out;

  Adder #(.width(32)) adder_1 (.a(rs1_data), .b(rs2_data), .out(adder_1_out));  // open: cin, cout
  assign rd_data = en ? adder_1_out : 32'bz;  // Controlled_Buffer controlled_buffer_1
endmodule

module LUI (
  input  en,
  input  [19:0] imm_data,
  output [31:0] rd_data
);

  assign rd_data = en ? {imm_data, {12{1'b0}}} : 32'bz;  // Controlled_Buffer controlled_buffer_1
endmodule

module LW (
  input  en,
  input  [31:0] rs_data,
  input  [11:0] offset,
  input  [31:0] memory_data,
  output [16:0] memory_addr,
  output [31:0] rd_data
);

  wire [31:0] adder_1_out, bit_extender_1_out, controlled_buffer_2_out;

  assign bit_extender_1_out = {{20{offset[11]}}, offset};  // Bit_Extender bit_extender_1
  Adder #(.width(32)) adder_1 (.a(rs_data), .b(bit_extender_1_out), .out(adder_1_out));  // open: cin, cout
  assign rd_data = en ? {memory_data[7:0], memory_data[15:8], memory_data[23:16], memory_data[31:24]} : 32'bz;  // Controlled_Buffer controlled_buffer_1
  assign {controlled_buffer_2_out[31:19], memory_addr, controlled_buffer_2_out[1:0]} = en ? adder_1_out : 32'bz;  // Controlled_Buffer controlled_buffer_2
endmodule

module SW (
  input  en,
  input  [31:0] rs1_data,
  input  [11:0] offset,
  input  [31:0] rs2_data,
  output [16:0] memory_addr,
  output [31:0] memory_data
);

  wire [31:0] adder_1_out, bit_extender_1_out, controlled_buffer_1_out;

  assign bit_extender_1_out = {{20{offset[11]}}, offset};  // Bit_Extender bit_extender_1
  Adder #(.width(32)) adder_1 (.a(rs1_data), .b(bit_extender_1_out), .out(adder_1_out));  // open: cin, cout
  assign {controlled_buffer_1_out[31:19], memory_addr, controlled_buffer_1_out[1:0]} = en ? adder_1_out : 32'bz;  // Controlled_Buffer controlled_buffer_1
  assign memory_data = en ? {rs2_data[7:0], rs2_data[15:8], rs2_data[23:16], rs2_data[31:24]} : 32'bz;  // Controlled_Buffer controlled_buffer_2
endmodule

module LBU (
  input  en,
  input  [31:0] rs_data,
  input  [11:0] offset,
  input  [31:0] memory_data,
  output [16:0] memory_addr,
  output [31:0] rd_data
);

  wire [7:0] bitselector_1_out;
  wire [31:0] adder_1_out, bit_extender_1_out, bit_extender_2_out, controlled_buffer_2_out;

  BitSelector #(.group(8), .width(32)) bitselector_1 (
    .in({memory_data[7:0], memory_data[15:8], memory_data[23:16], memory_data[31:24]}),
    .out(bitselector_1_out), .sel(controlled_buffer_2_out[1:0]));
  assign bit_extender_1_out = {{20{offset[11]}}, offset};  // Bit_Extender bit_extender_1
  Adder #(.width(32)) adder_1 (.a(rs_data), .b(bit_extender_1_out), .out(adder_1_out));  // open: cin, cout
  assign bit_extender_2_out = {{24{1'b0}}, bitselector_1_out};  // Bit_Extender bit_extender_2
  assign rd_data = en ? bit_extender_2_out : 32'bz;  // Controlled_Buffer controlled_buffer_1
  assign {controlled_buffer_2_out[31:19], memory_addr, controlled_buffer_2_out[1:0]} = en ? adder_1_out : 32'bz;  // Controlled_Buffer controlled_buffer_2
endmodule

module SB (
  input  en,
  input  [31:0] rs1_data,
  input  [11:0] offset,
  input  [31:0] rs2_data,
  output [3:0] byte_addr,
  output [16:0] memory_addr,
  output [31:0] memory_data,
  output byte_select
);

  wire [31:0] adder_1_out, bit_extender_1_out, controlled_buffer_1_out;

  assign bit_extender_1_out = {{20{offset[11]}}, offset};  // Bit_Extender bit_extender_1
  assign {controlled_buffer_1_out[31:19], memory_addr, controlled_buffer_1_out[1:0]} = en ? adder_1_out : 32'bz;  // Controlled_Buffer controlled_buffer_1
  Adder #(.width(32)) adder_1 (.a(rs1_data), .b(bit_extender_1_out), .out(adder_1_out));  // open: cin, cout
  assign memory_data = en ? {rs2_data[7:0], rs2_data[7:0], rs2_data[7:0], rs2_data[7:0]} : 32'bz;  // Controlled_Buffer controlled_buffer_2
  Decoder #(.select(2)) decoder_1 (
    .out0(byte_addr[0]), .out1(byte_addr[1]), .out2(byte_addr[2]), .out3(byte_addr[3]),
    .sel(controlled_buffer_1_out[1:0]));  // open: en

  assign byte_select = en;
endmodule
