// Logisim project sCPU.circ as structural Verilog: 7 circuits, main circuit main
module main (
  input  CLK
);

  wire [2:0] counter_8_1_y;
  wire [3:0] adder_1_out, multiplexer_1_out, ram4x4_new_1_rdata1, ram4x4_new_1_rdata2;
  wire [7:0] asyncrom8x8_1_out_2;

  counter_8 counter_8_1 (.CLK(CLK), .Y(counter_8_1_y));  // open: R, Cout
  asyncROM8x8 asyncrom8x8_1 (.address(counter_8_1_y), .out_2(asyncrom8x8_1_out_2));
  // Probe on asyncrom8x8_1_out_2
  Decoder #(.select(2)) decoder_1 (.sel(asyncrom8x8_1_out_2[7:6]));  // open: out0, out1, out2, out3, en
  Multiplexer #(.width(4)) multiplexer_1 (
    .in0(asyncrom8x8_1_out_2[3:0]), .in1(adder_1_out), .out(multiplexer_1_out));  // open: sel
  RAM4x4_new ram4x4_new_1 (
    .WADDR(asyncrom8x8_1_out_2[5:4]), .WDATA(multiplexer_1_out), .RADDR1(asyncrom8x8_1_out_2[1:0]),
    .RADDR2(asyncrom8x8_1_out_2[3:2]), .RDATA1(ram4x4_new_1_rdata1), .RDATA2(ram4x4_new_1_rdata2));  // open: WEN, CLK
  Adder #(.width(4)) adder_1 (.a(ram4x4_new_1_rdata1), .b(ram4x4_new_1_rdata2), .out(adder_1_out));  // open: cin, cout

  // Notes on the sheet:
  //   先做出两种指令，再利用多路选择器对结果进行筛选
endmodule

module asyncROM8x8 (
  input  [2:0] address,
  output [7:0] out_2
);

  Multiplexer #(.select(3), .width(8)) multiplexer_1 (
    .in0(8'h8a), .in1(8'h90), .in2(8'ha0), .in3(8'hb1), .in4(8'h17), .in5(8'h29), .in6(8'hd1), .in7(8'hdf),
    .out(out_2), .sel(address));

  // Notes on the sheet:
  //   li r0, 10
  //   li r1, 0
  //   li r2, 0
  //   li r3, 1
  //   add r1, r1, r3
  //   add r2, r2, r1
  //   bner0 r1, 4
  //   bner0 r3, 7
endmodule

module syncRAM8x8 (
  input  [2:0] ADDRESS,
  input  EN,
  input  CLK,
  input  [7:0] DATA_IN,
  input  WE,
  output [7:0] DATA_OUT
);

  wire [2:0] register_1_q;
  wire [7:0] register_2_q, register_3_q, register_4_q, register_5_q, register_6_q, register_7_q,
       register_8_q, register_9_q;
  wire [8:0] demultiplexer_1_out0, demultiplexer_1_out1, demultiplexer_1_out2, demultiplexer_1_out3,
       demultiplexer_1_out4, demultiplexer_1_out5, demultiplexer_1_out6, demultiplexer_1_out7;

  Demultiplexer #(.select(3), .width(9)) demultiplexer_1 (
    .out0(demultiplexer_1_out0), .out1(demultiplexer_1_out1), .out2(demultiplexer_1_out2),
    .out3(demultiplexer_1_out3), .out4(demultiplexer_1_out4), .out5(demultiplexer_1_out5),
    .out6(demultiplexer_1_out6), .out7(demultiplexer_1_out7), .in({WE, DATA_IN}), .sel(ADDRESS));
  Register #(.width(3)) register_1 (.D(ADDRESS), .en(EN), .clk(CLK), .Q(register_1_q));  // open: clr
  Register register_2 (
    .D(demultiplexer_1_out0[7:0]), .en(demultiplexer_1_out0[8]), .clk(CLK), .Q(register_2_q));  // open: clr
  Register register_3 (
    .D(demultiplexer_1_out1[7:0]), .en(demultiplexer_1_out1[8]), .clk(CLK), .Q(register_3_q));  // open: clr
  Register register_4 (
    .D(demultiplexer_1_out2[7:0]), .en(demultiplexer_1_out2[8]), .clk(CLK), .Q(register_4_q));  // open: clr
  Register register_5 (
    .D(demultiplexer_1_out3[7:0]), .en(demultiplexer_1_out3[8]), .clk(CLK), .Q(register_5_q));  // open: clr
  Register register_6 (
    .D(demultiplexer_1_out4[7:0]), .en(demultiplexer_1_out4[8]), .clk(CLK), .Q(register_6_q));  // open: clr
  Register register_7 (
    .D(demultiplexer_1_out5[7:0]), .en(demultiplexer_1_out5[8]), .clk(CLK), .Q(register_7_q));  // open: clr
  Register register_8 (
    .D(demultiplexer_1_out6[7:0]), .en(demultiplexer_1_out6[8]), .clk(CLK), .Q(register_8_q));  // open: clr
  Register register_9 (
    .D(demultiplexer_1_out7[7:0]), .en(demultiplexer_1_out7[8]), .clk(CLK), .Q(register_9_q));  // open: clr
  Multiplexer #(.select(3), .width(8)) multiplexer_1 (
    .in0(register_2_q), .in1(register_3_q), .in2(register_4_q), .in3(register_5_q), .in4(register_6_q),
    .in5(register_7_q), .in6(register_8_q), .in7(register_9_q), .out(DATA_OUT), .sel(register_1_q));
endmodule

module counter_8 (
  input  CLK,
  input  R,
  output Cout,
  output [2:0] Y
);

  wire [2:0] adder_1_out;

  D_Flip_Flop d_ff_1 (.D(adder_1_out[0]), .clk(CLK), .Q(Y[0]), .reset(R));  // open: Qn, preset
  D_Flip_Flop d_ff_2 (.D(adder_1_out[1]), .clk(CLK), .Q(Y[1]), .reset(R));  // open: Qn, preset
  D_Flip_Flop d_ff_3 (.D(adder_1_out[2]), .clk(CLK), .Q(Y[2]), .reset(R));  // open: Qn, preset
  Adder #(.width(3)) adder_1 (.a(Y), .b(3'b001), .out(adder_1_out), .cout(Cout));  // open: cin
endmodule

module syncRAM4x4 (
  input  [1:0] ADDRESS,
  input  EN,
  input  CLK,
  input  [3:0] DATA_IN,
  input  WE,
  output [3:0] DATA_OUT
);

  wire [1:0] register_1_q;
  wire [3:0] register_2_q, register_3_q, register_4_q, register_5_q;
  wire [4:0] demultiplexer_1_out0, demultiplexer_1_out1, demultiplexer_1_out2, demultiplexer_1_out3;

  Demultiplexer #(.select(2), .width(5)) demultiplexer_1 (
    .out0(demultiplexer_1_out0), .out1(demultiplexer_1_out1), .out2(demultiplexer_1_out2),
    .out3(demultiplexer_1_out3), .in({WE, DATA_IN}), .sel(ADDRESS));
  Register #(.width(2)) register_1 (.D(ADDRESS), .en(EN), .clk(CLK), .Q(register_1_q));  // open: clr
  Register #(.width(4)) register_2 (
    .D(demultiplexer_1_out0[3:0]), .en(demultiplexer_1_out0[4]), .clk(CLK), .Q(register_2_q));  // open: clr
  Register #(.width(4)) register_3 (
    .D(demultiplexer_1_out1[3:0]), .en(demultiplexer_1_out1[4]), .clk(CLK), .Q(register_3_q));  // open: clr
  Register #(.width(4)) register_4 (
    .D(demultiplexer_1_out2[3:0]), .en(demultiplexer_1_out2[4]), .clk(CLK), .Q(register_4_q));  // open: clr
  Register #(.width(4)) register_5 (
    .D(demultiplexer_1_out3[3:0]), .en(demultiplexer_1_out3[4]), .clk(CLK), .Q(register_5_q));  // open: clr
  Multiplexer #(.select(2), .width(4)) multiplexer_1 (
    .in0(register_2_q), .in1(register_3_q), .in2(register_4_q), .in3(register_5_q), .out(DATA_OUT),
    .sel(register_1_q));
endmodule

module sCPU_li (
  input  CLK,
  output [3:0] out_2
);

  wire decoder_1_out2;
  wire [2:0] counter_8_1_y;
  wire [7:0] asyncrom8x8_1_out_2;

  counter_8 counter_8_1 (.CLK(CLK), .Y(counter_8_1_y));  // open: R, Cout
  // Probe on counter_8_1_y
  asyncROM8x8 asyncrom8x8_1 (.address(counter_8_1_y), .out_2(asyncrom8x8_1_out_2));
  // Probe on asyncrom8x8_1_out_2
  Decoder #(.select(2)) decoder_1 (
    .out2(decoder_1_out2), .sel(asyncrom8x8_1_out_2[7:6]));  // open: out0, out1, out3, en
  syncRAM4x4 syncram4x4_1 (
    .ADDRESS(asyncrom8x8_1_out_2[5:4]), .EN(decoder_1_out2), .CLK(CLK), .DATA_IN(asyncrom8x8_1_out_2[3:0]),
    .WE(decoder_1_out2), .DATA_OUT(out_2));
endmodule

module RAM4x4_new (
  input  [1:0] WADDR,
  input  [3:0] WDATA,
  input  WEN,
  input  CLK,
  input  [1:0] RADDR1,
  input  [1:0] RADDR2,
  output [3:0] RDATA1,
  output [3:0] RDATA2
);

  wire [3:0] register_1_q, register_2_q, register_3_q, register_4_q;
  wire [4:0] demultiplexer_1_out0, demultiplexer_1_out1, demultiplexer_1_out2, demultiplexer_1_out3;

  Demultiplexer #(.select(2), .width(5)) demultiplexer_1 (
    .out0(demultiplexer_1_out0), .out1(demultiplexer_1_out1), .out2(demultiplexer_1_out2),
    .out3(demultiplexer_1_out3), .in({WEN, WDATA}), .sel(WADDR));
  Register #(.width(4)) register_1 (
    .D(demultiplexer_1_out0[3:0]), .en(demultiplexer_1_out0[4]), .clk(CLK), .Q(register_1_q));  // open: clr
  Register #(.width(4)) register_2 (
    .D(demultiplexer_1_out1[3:0]), .en(demultiplexer_1_out1[4]), .clk(CLK), .Q(register_2_q));  // open: clr
  Register #(.width(4)) register_3 (
    .D(demultiplexer_1_out2[3:0]), .en(demultiplexer_1_out2[4]), .clk(CLK), .Q(register_3_q));  // open: clr
  Register #(.width(4)) register_4 (
    .D(demultiplexer_1_out3[3:0]), .en(demultiplexer_1_out3[4]), .clk(CLK), .Q(register_4_q));  // open: clr
  Multiplexer #(.select(2), .width(4)) multiplexer_1 (
    .in0(register_4_q), .in1(register_3_q), .in2(register_2_q), .in3(register_1_q), .out(RDATA1), .sel(RADDR1));
  Multiplexer #(.select(2), .width(4)) multiplexer_2 (
    .in0(register_1_q), .in1(register_2_q), .in2(register_3_q), .in3(register_4_q), .out(RDATA2), .sel(RADDR2));
endmodule
